// Logisim project LOgic circuit.circ as structural Verilog: 19 circuits
module main (
  input  in_1,
  input  in_2,
  output [6:0] out_3,
  output [4:0] out_4,
  output [2:0] out_5,
  output [4:0] out_6,
  output [4:0] out_7,
  output [6:0] out_8
);

  wire control_decode_p1, control_decode_p2, control_decode_p3, control_decode_p4, Data_Memory_p3,
       Register_file_p2, Register_file_p4, text_1_p2, text_1_p3, text_1_p6, text_1_p7, text_1_p13,
       text_1_p14, text_1_p16, text_1_p17, text_1_p18, text_1_p21, text_1_p22, text_1_p24, text_1_p25,
       text_2_p1, text_7_p3, text_7_p4, text_7_p5, text_8_p2, text_8_p5, text_8_p8, text_8_p12, text_8_p13,
       text_8_p15, text_8_p17, text_8_p18, text_9_p3, text_9_p4, text_9_p6, text_9_p8, text_10_p2,
       text_10_p4, undriven, undriven_3, undriven_4, undriven_5;
  wire [2:0] text_8_p11;
  wire [3:0] TYPE_DECODER_out_2;
  wire [6:0] text_1_p5, text_7_p1;
  wire [24:7] text_4_p1;
  wire [25:2] undriven_2;
  wire [31:0] adder_2_out, Data_Memory_p5, Data_Memory_p6, multiplexer_2_out, multiplexer_4_out,
       register_1_q, text_1_p9, text_1_p10, text_1_p15, text_8_p6, text_8_p10, text_8_p14, text_9_p9,
       text_10_p5, undriven_6;

  Register #(.width(32)) register_1 (.en(in_1), .Q(register_1_q), .clk(undriven));  // open: D, clr
  Clock clock_1 ();  // open: out
  // control_decode control_decode: pin names not known; wires that end beside it: control_decode_p1, control_decode_p2, control_decode_p3, control_decode_p4
  // Text text_1: pin names not known; wires that end beside it: in_2, text_1_p2, text_1_p3, in_2, text_1_p5, text_1_p6, text_1_p7, text_1_p2, text_1_p9, text_1_p10, control_decode_p1, text_1_p10[6:0], text_1_p13, text_1_p14, text_1_p15, text_1_p16, text_1_p17, text_1_p18, text_1_p18, text_1_p10[24:20], text_1_p21, text_1_p22, control_decode_p3, text_1_p24, text_1_p25
  RAM #(.addrWidth(24), .dataWidth(32)) ram_1 (
    .addr(undriven_2), .data(text_1_p9), .sel(text_1_p3), .clr(in_2));  // open: clk, ld
  // Text text_2: pin names not known; wires that end beside it: text_2_p1, out_3
  // Text text_3: pin names not known; wires that end beside it: text_2_p1, out_4
  // Text text_4: pin names not known; wires that end beside it: text_4_p1[11:7], text_4_p1[19:15], out_5
  // Text text_5: pin names not known; wires that end beside it: out_6
  // Text text_6: pin names not known; wires that end beside it: text_4_p1[24:20], out_7
  // Text text_7: pin names not known; wires that end beside it: text_7_p1, text_1_p14, text_7_p3, text_7_p4, text_7_p5, text_7_p5, text_1_p7, text_7_p4, text_1_p17
  immediate_gen_3 immediate_gen_3_1 (.IMM(text_1_p15));  // open: ins
  Type_decoder TYPE_DECODER (.OP_CODE(text_1_p5), .out_2(TYPE_DECODER_out_2), .out_3(text_1_p13));
  // Register_File Register_file: pin names not known; wires that end beside it: text_1_p21, Register_file_p2, text_1_p22, Register_file_p4
  ALU_CONTROL ALUControl (.OPCODE(text_7_p1));  // open: FUNCT_3, FUNCT_7, in_4, OUTPUT
  // Text text_8: pin names not known; wires that end beside it: text_1_p25, text_8_p2, Register_file_p4, Register_file_p4, text_8_p5, text_8_p6, text_8_p2, text_8_p8, text_8_p8, text_8_p10, text_8_p11, text_8_p12, text_8_p13, text_8_p14, text_8_p15, text_8_p15, text_8_p17, text_8_p18, text_8_p18
  Multiplexer #(.width(32), .enable("false")) multiplexer_1 (.in1(text_8_p6), .sel(text_8_p5));  // open: in0, out
  ALU_With_branch ALU_With_Branch (
    .A(text_8_p10), .BranchType(text_8_p11), .out_6(text_8_p14));  // open: B, ALUOp, out_5
  Multiplexer #(.width(32), .enable("false")) multiplexer_2 (
    .out(multiplexer_2_out), .sel(undriven_4));  // open: in0, in1
  // AND_Gate and_1 has open pins: in0=control_decode_p4, in1=undriven_3, out=open
  // Text text_9: pin names not known; wires that end beside it: multiplexer_2_out, text_7_p3, text_9_p3, text_9_p4, text_1_p24, text_9_p6, text_9_p6, text_9_p8, text_9_p9
  // Data_Memory Data_Memory: pin names not known; wires that end beside it: text_8_p13, text_9_p3, Data_Memory_p3, text_9_p4, Data_Memory_p5, Data_Memory_p6
  // OR_Gate or_1 has open pins: in1=undriven_5, out=open
  Multiplexer #(.width(32), .enable("false")) multiplexer_3 (
    .in0(Data_Memory_p5), .in1(Data_Memory_p6));  // open: out, sel
  Adder #(.width(32)) adder_1 (.a(32'h4), .out(text_9_p9));  // open: b, cin, cout
  Adder #(.width(32)) adder_2 (.a(undriven_6), .out(adder_2_out));  // open: b, cin, cout
  // Text text_10: pin names not known; wires that end beside it: text_9_p8, text_10_p2, text_9_p9, text_10_p4, text_10_p5, text_10_p2
  Multiplexer #(.width(32), .enable("false")) multiplexer_4 (
    .in0(text_10_p5), .out(multiplexer_4_out));  // open: in1, sel
  // OR_Gate or_2 is placed but not wired

  // Notes on the sheet:
  //   contents of ram_1 (hex, n*v repeats v):
  //   84000117     00010113     008000ef     0000006f     fb010113     800005b7     03312e23     00058993
  //   01898393     04112623     04812423     04912223     05212023     03412c23     03512a23     03612823
  //   03712623     03812423     03912223     03a12023     01b12e23     00058593     14498f13     00038713
  //   02000693     00a00613     fe870793     00d78023     00178793     fee79ce3     00c78023     01978713
  //   ffe714e3     2d2d3737     00098793     d2d70713     00e7a023     00478793     fef39ce3     00b78713
  //   00a78793     00c00713     00b00793     00b00713     01000793     00c00713     00b00793     00b00713
  //   02000793     00c00713     00b00793     00b00713     00c00793     00b00713     00b00793     00c00713
  //   00b00793     00b00713     00c00793     00b00713     00b00793     00c00713     00b00793     00b00713
  //   00c00793     00b00713     00b00793     00c00713     00b00793     00b00713     00c00793     00b00713
  //   00b00793     00c00713     00b00793     00b00713     00c00793     00b00713     00b00793     00c00713
  //   00b00793     00b00713     00c00793     00b00713     00b00793     00c00713     00b00793     00b00713
endmodule

module immediate_generation (
  input  [31:0] in_1,
  input  [31:0] in_2,
  input  [2:0] in_3,
  output [31:0] out_4
);

  wire [19:0] shifter_1_out;
  wire [31:0] adder_1_out, adder_2_out, bit_extender_1_out, bit_extender_2_out, bit_extender_3_out,
       bit_extender_4_out, bit_extender_5_out;

  // Text text_1: pin names not known
  // Text text_2: pin names not known
  Shifter #(.width(20)) shifter_1 (.in(in_2[31:12]), .\dist (5'b01100), .out(shifter_1_out));
  assign bit_extender_1_out = {{20{in_2[31]}}, in_2[31:20]};  // Bit_Extender bit_extender_1
  assign bit_extender_2_out = {{20{in_2[31]}}, {in_2[31:25], in_2[11:7]}};  // Bit_Extender bit_extender_2
  assign bit_extender_3_out = {{19{in_2[31]}}, {in_2[31], in_2[7], in_2[30:25], in_2[11:8], 1'b0}};  // Bit_Extender bit_extender_3
  assign bit_extender_4_out = {{11{in_2[31]}}, {in_2[31], in_2[19:12], in_2[20], in_2[30:21], 1'b0}};  // Bit_Extender bit_extender_4
  assign bit_extender_5_out = {{12{shifter_1_out[19]}}, shifter_1_out};  // Bit_Extender bit_extender_5
  Adder #(.width(32)) adder_1 (.a(bit_extender_3_out), .b(in_1), .out(adder_1_out));  // open: cin, cout
  Adder #(.width(32)) adder_2 (.a(bit_extender_4_out), .b(in_1), .out(adder_2_out));  // open: cin, cout
  Multiplexer #(.select(3), .width(32), .enable("false")) multiplexer_1 (
    .in1(bit_extender_1_out), .in2(bit_extender_2_out), .in3(adder_1_out), .in4(adder_2_out),
    .in5(bit_extender_5_out), .out(out_4), .sel(in_3));  // open: in0, in6, in7
endmodule

module instruction_decoder (
  input  [31:0] in_1,
  output [6:0] out_2,
  output [4:0] out_3,
  output [2:0] out_4,
  output [4:0] out_5,
  output [4:0] out_6,
  output [6:0] out_7
);

  // Text text_1: pin names not known
  // Text text_2: pin names not known
  // Text text_3: pin names not known
  // Text text_4: pin names not known
  // Text text_5: pin names not known
  // Text text_6: pin names not known

  assign out_2 = in_1[6:0];
  assign out_3 = in_1[11:7];
  assign out_4 = in_1[14:12];
  assign out_5 = in_1[19:15];
  assign out_6 = in_1[24:20];
  assign out_7 = in_1[31:25];
endmodule

module control_decode (
  input  [6:0] in_1,
  output out_2,
  output out_3,
  output [1:0] out_4,
  output out_5,
  output out_6,
  output out_7,
  output out_8,
  output out_9
);

  wire comparator_1_eq, comparator_2_eq, comparator_3_eq, comparator_4_eq, comparator_5_eq, comparator_6_eq,
       comparator_7_eq, comparator_8_eq, comparator_9_eq;
  wire [1:0] bit_extender_1_out, bit_extender_2_out;

  Comparator #(.width(7)) comparator_1 (.a(in_1), .b(7'b0110011), .eq(comparator_1_eq));  // open: gt, lt
  Comparator #(.width(7)) comparator_2 (.a(in_1), .b(7'b0010011), .eq(comparator_2_eq));  // open: gt, lt
  Comparator #(.width(7)) comparator_3 (.a(in_1), .b(7'b0000011), .eq(comparator_3_eq));  // open: gt, lt
  Comparator #(.width(7)) comparator_4 (.a(in_1), .b(7'b1101111), .eq(comparator_4_eq));  // open: gt, lt
  Comparator #(.width(7)) comparator_5 (.a(in_1), .b(7'b0010011), .eq(comparator_5_eq));  // open: gt, lt
  Comparator #(.width(7)) comparator_6 (.a(in_1), .b(7'b0000011), .eq(comparator_6_eq));  // open: gt, lt
  Comparator #(.width(7)) comparator_7 (.a(in_1), .b(7'b0100011), .eq(comparator_7_eq));  // open: gt, lt
  Comparator #(.width(7)) comparator_8 (.a(in_1), .b(7'b0110011), .eq(comparator_8_eq));  // open: gt, lt
  Comparator #(.width(7)) comparator_9 (.a(in_1), .b(7'b1100011), .eq(comparator_9_eq));  // open: gt, lt
  Comparator #(.width(7)) comparator_10 (.a(in_1), .b(7'b0000011), .eq(out_5));  // open: gt, lt
  Comparator #(.width(7)) comparator_11 (.a(in_1), .b(7'b0100011), .eq(out_6));  // open: gt, lt
  Comparator #(.width(7)) comparator_12 (.a(in_1), .b(7'b0000011), .eq(out_7));  // open: gt, lt
  Comparator #(.width(7)) comparator_13 (.a(in_1), .b(7'b1100011), .eq(out_8));  // open: gt, lt
  Comparator #(.width(7)) comparator_14 (.a(in_1), .b(7'b1101111), .eq(out_9));  // open: gt, lt
  or or_1 (out_2, comparator_1_eq, comparator_2_eq, comparator_3_eq, comparator_4_eq);
  or or_2 (out_3, comparator_5_eq, comparator_6_eq, comparator_7_eq);
  assign bit_extender_1_out = {{1{1'b0}}, comparator_8_eq};  // Bit_Extender bit_extender_1
  assign bit_extender_2_out = {{1{1'b0}}, comparator_9_eq};  // Bit_Extender bit_extender_2
  // Text text_1: pin names not known
  // Text text_2: pin names not known
  // Text text_3: pin names not known
  // Text text_4: pin names not known
  // Text text_5: pin names not known
  // Text text_6: pin names not known
  // Text text_7: pin names not known
  assign out_4 = bit_extender_1_out | bit_extender_2_out;  // OR_Gate or_3, 2 bits wide
  // Text text_8: pin names not known
endmodule

module Register_File (
  input  [31:0] WriteData,
  input  in_2,
  input  [4:0] ReadReg1,
  input  RegWrite,
  input  [4:0] WriteReg,
  input  [4:0] ReadReg2,
  input  clr,
  output [31:0] Read_Data1,
  output [31:0] Read_Data2
);

  wire and_1_out, decoder_1_out0, decoder_1_out1, decoder_1_out2, decoder_1_out3, decoder_1_out4,
       decoder_1_out5, decoder_1_out6, decoder_1_out7, decoder_1_out8, decoder_1_out9, decoder_1_out10,
       decoder_1_out11, decoder_1_out12, decoder_1_out13, decoder_1_out14, decoder_1_out15, decoder_1_out16,
       decoder_1_out17, decoder_1_out18, decoder_1_out19, decoder_1_out20, decoder_1_out21, decoder_1_out22,
       decoder_1_out23, decoder_1_out24, decoder_1_out25, decoder_1_out26, decoder_1_out27, decoder_1_out28,
       decoder_1_out29, decoder_1_out30, decoder_1_out31;
  wire [31:0] multiplexer_1_out, R0_q, R1_q, R2_q, R3_q, R4_q, R5_q, R6_q, R7_q, R8_q, R9_q, R10_q, R11_q,
       R12_q, R13_q, R14_q, R15_q, R16_q, R17_q, R18_q, R19_q, R20_q, R21_q, R22_q, R23_q, R24_q, R25_q,
       R26_q, R27_q, R28_q, R29_q, R30_q, R31_q;

  Decoder #(.select(5), .enable("false")) decoder_1 (
    .out0(decoder_1_out0), .out1(decoder_1_out1), .out2(decoder_1_out2), .out3(decoder_1_out3),
    .out4(decoder_1_out4), .out5(decoder_1_out5), .out6(decoder_1_out6), .out7(decoder_1_out7),
    .out8(decoder_1_out8), .out9(decoder_1_out9), .out10(decoder_1_out10), .out11(decoder_1_out11),
    .out12(decoder_1_out12), .out13(decoder_1_out13), .out14(decoder_1_out14), .out15(decoder_1_out15),
    .out16(decoder_1_out16), .out17(decoder_1_out17), .out18(decoder_1_out18), .out19(decoder_1_out19),
    .out20(decoder_1_out20), .out21(decoder_1_out21), .out22(decoder_1_out22), .out23(decoder_1_out23),
    .out24(decoder_1_out24), .out25(decoder_1_out25), .out26(decoder_1_out26), .out27(decoder_1_out27),
    .out28(decoder_1_out28), .out29(decoder_1_out29), .out30(decoder_1_out30), .out31(decoder_1_out31),
    .sel(WriteReg));
  Multiplexer #(.width(32), .enable("false")) multiplexer_1 (
    .in1(WriteData), .out(multiplexer_1_out), .sel(RegWrite));  // open: in0
  and and_1 (and_1_out, 1'b0, decoder_1_out0);
  Register #(.width(32)) R0 (.D(multiplexer_1_out), .en(and_1_out), .Q(R0_q), .clk(in_2), .clr(clr));
  Register #(.width(32)) R1 (.D(multiplexer_1_out), .en(decoder_1_out1), .Q(R1_q), .clk(in_2), .clr(clr));
  Register #(.width(32)) R8 (.D(multiplexer_1_out), .en(decoder_1_out8), .Q(R8_q), .clk(in_2), .clr(clr));
  Register #(.width(32)) R2 (.D(multiplexer_1_out), .en(decoder_1_out2), .Q(R2_q), .clk(in_2), .clr(clr));
  Register #(.width(32)) R9 (.D(multiplexer_1_out), .en(decoder_1_out9), .Q(R9_q), .clk(in_2), .clr(clr));
  Register #(.width(32)) R16 (.D(multiplexer_1_out), .en(decoder_1_out16), .Q(R16_q), .clk(in_2), .clr(clr));
  Register #(.width(32)) R3 (.D(multiplexer_1_out), .en(decoder_1_out3), .Q(R3_q), .clk(in_2), .clr(clr));
  Register #(.width(32)) R10 (.D(multiplexer_1_out), .en(decoder_1_out10), .Q(R10_q), .clk(in_2), .clr(clr));
  Register #(.width(32)) R17 (.D(multiplexer_1_out), .en(decoder_1_out17), .Q(R17_q), .clk(in_2), .clr(clr));
  Register #(.width(32)) R24 (.D(multiplexer_1_out), .en(decoder_1_out24), .Q(R24_q), .clk(in_2), .clr(clr));
  Register #(.width(32)) R4 (.D(multiplexer_1_out), .en(decoder_1_out4), .Q(R4_q), .clk(in_2), .clr(clr));
  Register #(.width(32)) R11 (.D(multiplexer_1_out), .en(decoder_1_out11), .Q(R11_q), .clk(in_2), .clr(clr));
  Register #(.width(32)) R18 (.D(multiplexer_1_out), .en(decoder_1_out18), .Q(R18_q), .clk(in_2), .clr(clr));
  Register #(.width(32)) R25 (.D(multiplexer_1_out), .en(decoder_1_out25), .Q(R25_q), .clk(in_2), .clr(clr));
  Register #(.width(32)) R5 (.D(multiplexer_1_out), .en(decoder_1_out5), .Q(R5_q), .clk(in_2), .clr(clr));
  Register #(.width(32)) R6 (.D(multiplexer_1_out), .en(decoder_1_out6), .Q(R6_q), .clk(in_2), .clr(clr));
  Register #(.width(32)) R12 (.D(multiplexer_1_out), .en(decoder_1_out12), .Q(R12_q), .clk(in_2), .clr(clr));
  Register #(.width(32)) R19 (.D(multiplexer_1_out), .en(decoder_1_out19), .Q(R19_q), .clk(in_2), .clr(clr));
  Register #(.width(32)) R26 (.D(multiplexer_1_out), .en(decoder_1_out26), .Q(R26_q), .clk(in_2), .clr(clr));
  Register #(.width(32)) R7 (.D(multiplexer_1_out), .en(decoder_1_out7), .Q(R7_q), .clk(in_2), .clr(clr));
  Register #(.width(32)) R13 (.D(multiplexer_1_out), .en(decoder_1_out13), .Q(R13_q), .clk(in_2), .clr(clr));
  Register #(.width(32)) R14 (.D(multiplexer_1_out), .en(decoder_1_out14), .Q(R14_q), .clk(in_2), .clr(clr));
  Register #(.width(32)) R20 (.D(multiplexer_1_out), .en(decoder_1_out20), .Q(R20_q), .clk(in_2), .clr(clr));
  Register #(.width(32)) R27 (.D(multiplexer_1_out), .en(decoder_1_out27), .Q(R27_q), .clk(in_2), .clr(clr));
  Register #(.width(32)) R28 (.D(multiplexer_1_out), .en(decoder_1_out28), .Q(R28_q), .clk(in_2), .clr(clr));
  Register #(.width(32), .trigger("falling")) R15 (
    .D(multiplexer_1_out), .en(decoder_1_out15), .Q(R15_q), .clk(in_2), .clr(clr));
  Register #(.width(32)) R21 (.D(multiplexer_1_out), .en(decoder_1_out21), .Q(R21_q), .clk(in_2), .clr(clr));
  Register #(.width(32)) R22 (.D(multiplexer_1_out), .en(decoder_1_out22), .Q(R22_q), .clk(in_2), .clr(clr));
  Register #(.width(32)) R29 (.D(multiplexer_1_out), .en(decoder_1_out29), .Q(R29_q), .clk(in_2), .clr(clr));
  Register #(.width(32)) R23 (.D(multiplexer_1_out), .en(decoder_1_out23), .Q(R23_q), .clk(in_2), .clr(clr));
  Register #(.width(32)) R30 (.D(multiplexer_1_out), .en(decoder_1_out30), .Q(R30_q), .clk(in_2), .clr(clr));
  Register #(.width(32)) R31 (.D(multiplexer_1_out), .en(decoder_1_out31), .Q(R31_q), .clk(in_2), .clr(clr));
  Multiplexer #(.select(5), .width(32), .enable("false")) multiplexer_2 (
    .in0(R0_q), .in1(R1_q), .in2(R2_q), .in3(R3_q), .in4(R4_q), .in5(R5_q), .in6(R6_q), .in7(R7_q),
    .in8(R8_q), .in9(R9_q), .in10(R10_q), .in11(R11_q), .in12(R12_q), .in13(R13_q), .in14(R14_q),
    .in15(R15_q), .in16(R16_q), .in17(R17_q), .in18(R18_q), .in19(R19_q), .in20(R20_q), .in21(R21_q),
    .in22(R22_q), .in23(R23_q), .in24(R24_q), .in25(R25_q), .in26(R26_q), .in27(R27_q), .in28(R28_q),
    .in29(R29_q), .in30(R30_q), .in31(R31_q), .out(Read_Data1), .sel(ReadReg1));
  Multiplexer #(.select(5), .width(32), .enable("false")) multiplexer_3 (
    .in0(R0_q), .in1(R1_q), .in2(R2_q), .in3(R3_q), .in4(R4_q), .in5(R5_q), .in6(R6_q), .in7(R7_q),
    .in8(R8_q), .in9(R9_q), .in10(R10_q), .in11(R11_q), .in12(R12_q), .in13(R13_q), .in14(R14_q),
    .in15(R15_q), .in16(R16_q), .in17(R17_q), .in18(R18_q), .in19(R19_q), .in20(R20_q), .in21(R21_q),
    .in22(R22_q), .in23(R23_q), .in24(R24_q), .in25(R25_q), .in26(R26_q), .in27(R27_q), .in28(R28_q),
    .in29(R29_q), .in30(R30_q), .in31(R31_q), .out(Read_Data2), .sel(ReadReg2));
endmodule

module Type_decoder (
  input  [6:0] OP_CODE,
  output [3:0] out_2,
  output out_3
);

  wire comparator_2_eq, comparator_3_eq, comparator_4_eq, comparator_5_eq, comparator_7_eq;
  wire [2:0] T0_out;

  // Text text_1: pin names not known
  // Text text_2: pin names not known
  // Text text_3: pin names not known
  // Text text_4: pin names not known
  // Text text_5: pin names not known
  // Text text_6: pin names not known
  // Text text_7: pin names not known
  Comparator #(.width(7)) comparator_1 (.a(OP_CODE), .b(7'b0110011));  // open: gt, eq, lt
  Comparator #(.width(7)) comparator_2 (.a(OP_CODE), .b(7'b0010011), .eq(comparator_2_eq));  // open: gt, lt
  Comparator #(.width(7)) comparator_3 (.a(OP_CODE), .b(7'b0100011), .eq(comparator_3_eq));  // open: gt, lt
  Comparator #(.width(7)) comparator_4 (.a(OP_CODE), .b(7'b1100011), .eq(comparator_4_eq));  // open: gt, lt
  Comparator #(.width(7)) comparator_5 (.a(OP_CODE), .b(7'b0110111), .eq(comparator_5_eq));  // open: gt, lt
  Comparator #(.width(7)) comparator_6 (.a(OP_CODE), .b(7'b1101111), .eq(out_3));  // open: gt, lt
  Comparator #(.width(7)) comparator_7 (.a(OP_CODE), .b(7'b0010001), .eq(comparator_7_eq));  // open: gt, lt
  or T0 (T0_out[0], comparator_2_eq, comparator_4_eq, out_3);
  or T1 (T0_out[1], comparator_4_eq, comparator_3_eq, comparator_7_eq);
  or T2 (T0_out[2], comparator_7_eq, out_3, comparator_5_eq);
  assign out_2 = {{1{1'b0}}, T0_out};  // Bit_Extender bit_extender_1
endmodule

module ALU_CONTROL (
  input  [6:0] OPCODE,
  input  [2:0] FUNCT_3,
  input  [6:0] FUNCT_7,
  input  [3:0] in_4,
  output [3:0] OUTPUT
);

  wire add_out, AND_out, BEQ_out, comparator_1_eq, comparator_2_eq, comparator_3_eq, comparator_4_eq,
       comparator_5_eq, comparator_6_eq, comparator_7_eq, comparator_8_eq, comparator_9_eq, comparator_10_eq,
       comparator_11_eq, comparator_12_eq, comparator_13_eq, comparator_14_eq, comparator_15_eq,
       comparator_16_eq, comparator_17_eq, comparator_18_eq, comparator_19_eq, comparator_20_eq,
       comparator_21_eq, comparator_22_eq, comparator_23_eq, comparator_24_eq, comparator_25_eq,
       comparator_26_eq, comparator_27_eq, comparator_28_eq, comparator_29_eq, comparator_30_eq,
       comparator_31_eq, comparator_32_eq, comparator_33_eq, comparator_34_eq, comparator_35_eq,
       comparator_36_eq, comparator_37_eq, comparator_38_eq, comparator_39_eq, comparator_40_eq,
       comparator_41_eq, LW_SW_out, or_1_out, OR_2_out, or_3_out, SLL_out, SLT_out, SLTU_out, SRA_out,
       SRL_out, sub_out, XOR_out;
  wire [3:0] bit_extender_1_out, bit_extender_2_out, bit_extender_3_out, bit_extender_4_out,
       bit_extender_5_out, bit_extender_6_out, bit_extender_7_out, bit_extender_8_out, bit_extender_9_out,
       bit_extender_10_out, bit_extender_11_out, bit_extender_12_out;

  Comparator #(.width(7)) comparator_1 (.a(OPCODE), .b(7'b0110011), .eq(comparator_1_eq));  // open: gt, lt
  Comparator #(.width(7)) comparator_2 (.a(OPCODE), .b(7'b0010011), .eq(comparator_2_eq));  // open: gt, lt
  Comparator #(.width(3)) comparator_3 (.a(FUNCT_3), .b(3'b000), .eq(comparator_3_eq));  // open: gt, lt
  Comparator #(.width(7)) comparator_4 (.a(FUNCT_7), .b({7{1'b0}}), .eq(comparator_4_eq));  // open: gt, lt
  Comparator #(.width(7)) comparator_5 (.a(OPCODE), .b(7'b0110011), .eq(comparator_5_eq));  // open: gt, lt
  Comparator #(.width(3)) comparator_6 (.a(FUNCT_3), .b(3'b000), .eq(comparator_6_eq));  // open: gt, lt
  Comparator #(.width(7)) comparator_7 (.a(FUNCT_7), .b(7'b0100000), .eq(comparator_7_eq));  // open: gt, lt
  Comparator #(.width(7)) comparator_8 (.a(OPCODE), .b(7'b0110011), .eq(comparator_8_eq));  // open: gt, lt
  Comparator #(.width(3)) comparator_9 (.a(FUNCT_3), .b(3'b111), .eq(comparator_9_eq));  // open: gt, lt
  Comparator #(.width(7)) comparator_10 (.a(FUNCT_7), .b({7{1'b0}}), .eq(comparator_10_eq));  // open: gt, lt
  Comparator #(.width(7)) comparator_11 (.a(OPCODE), .b(7'b0010011), .eq(comparator_11_eq));  // open: gt, lt
  Comparator #(.width(3)) comparator_12 (.a(FUNCT_3), .b(3'b111), .eq(comparator_12_eq));  // open: gt, lt
  Comparator #(.width(7)) comparator_13 (.a(OPCODE), .b(7'b0110011), .eq(comparator_13_eq));  // open: gt, lt
  Comparator #(.width(3)) comparator_14 (.a(FUNCT_3), .b(3'b110), .eq(comparator_14_eq));  // open: gt, lt
  Comparator #(.width(7)) comparator_15 (.a(FUNCT_7), .b({7{1'b0}}), .eq(comparator_15_eq));  // open: gt, lt
  Comparator #(.width(7)) comparator_16 (.a(OPCODE), .b(7'b0010011), .eq(comparator_16_eq));  // open: gt, lt
  Comparator #(.width(3)) comparator_17 (.a(FUNCT_3), .b(3'b000), .eq(comparator_17_eq));  // open: gt, lt
  Comparator #(.width(7)) comparator_18 (.a(OPCODE), .b(7'b0110011), .eq(comparator_18_eq));  // open: gt, lt
  Comparator #(.width(3)) comparator_19 (.a(FUNCT_3), .b(3'b100), .eq(comparator_19_eq));  // open: gt, lt
  Comparator #(.width(7)) comparator_20 (.a(FUNCT_7), .b({7{1'b0}}), .eq(comparator_20_eq));  // open: gt, lt
  Comparator #(.width(7)) comparator_21 (.a(OPCODE), .b(7'b0010011), .eq(comparator_21_eq));  // open: gt, lt
  Comparator #(.width(3)) comparator_22 (.a(FUNCT_3), .b(3'b100), .eq(comparator_22_eq));  // open: gt, lt
  Comparator #(.width(7)) comparator_23 (.a(OPCODE), .b(7'b0110011), .eq(comparator_23_eq));  // open: gt, lt
  Comparator #(.width(3)) comparator_24 (.a(FUNCT_3), .b(3'b001), .eq(comparator_24_eq));  // open: gt, lt
  Comparator #(.width(7)) comparator_25 (.a(FUNCT_7), .b({7{1'b0}}), .eq(comparator_25_eq));  // open: gt, lt
  Comparator #(.width(7)) comparator_26 (.a(OPCODE), .b(7'b0110011), .eq(comparator_26_eq));  // open: gt, lt
  Comparator #(.width(3)) comparator_27 (.a(FUNCT_3), .b(3'b011), .eq(comparator_27_eq));  // open: gt, lt
  Comparator #(.width(7)) comparator_28 (.a(FUNCT_7), .b({7{1'b0}}), .eq(comparator_28_eq));  // open: gt, lt
  Comparator #(.width(7)) comparator_29 (.a(OPCODE), .b(7'b0110011), .eq(comparator_29_eq));  // open: gt, lt
  Comparator #(.width(3)) comparator_30 (.a(FUNCT_3), .b(3'b101), .eq(comparator_30_eq));  // open: gt, lt
  Comparator #(.width(7)) comparator_31 (.a(FUNCT_7), .b(7'b0100000), .eq(comparator_31_eq));  // open: gt, lt
  Comparator #(.width(7)) comparator_32 (.a(OPCODE), .b(7'b0110011), .eq(comparator_32_eq));  // open: gt, lt
  Comparator #(.width(3)) comparator_33 (.a(FUNCT_3), .b(3'b010), .eq(comparator_33_eq));  // open: gt, lt
  Comparator #(.width(7)) comparator_34 (.a(FUNCT_7), .b({7{1'b0}}), .eq(comparator_34_eq));  // open: gt, lt
  Comparator #(.width(7)) comparator_35 (.a(OPCODE), .b(7'b0110011), .eq(comparator_35_eq));  // open: gt, lt
  Comparator #(.width(3)) comparator_36 (.a(FUNCT_3), .b(3'b011), .eq(comparator_36_eq));  // open: gt, lt
  Comparator #(.width(7)) comparator_37 (.a(FUNCT_7), .b({7{1'b0}}), .eq(comparator_37_eq));  // open: gt, lt
  Comparator #(.width(7)) comparator_38 (.a(OPCODE), .b(7'b1100011), .eq(comparator_38_eq));  // open: gt, lt
  Comparator #(.width(3)) comparator_39 (.a(3'b000), .b(FUNCT_3), .eq(comparator_39_eq));  // open: gt, lt
  Comparator #(.width(7)) comparator_40 (.a(OPCODE), .b(7'b0000011), .eq(comparator_40_eq));  // open: gt, lt
  Comparator #(.width(7)) comparator_41 (.a(OPCODE), .b(7'b0100011), .eq(comparator_41_eq));  // open: gt, lt
  // Text text_1: pin names not known
  or or_1 (or_1_out, comparator_1_eq, comparator_2_eq);
  and add (add_out, comparator_3_eq, comparator_4_eq);
  and sub (sub_out, comparator_5_eq, comparator_6_eq, comparator_7_eq);
  and AND (AND_out, comparator_8_eq, comparator_9_eq, comparator_10_eq, comparator_11_eq, comparator_12_eq);
  and OR_2 (OR_2_out, comparator_13_eq, comparator_14_eq, comparator_15_eq, comparator_16_eq, comparator_17_eq);
  and XOR (XOR_out, comparator_18_eq, comparator_19_eq, comparator_20_eq, comparator_21_eq, comparator_22_eq);
  and SLL (SLL_out, comparator_23_eq, comparator_24_eq, comparator_25_eq);
  and SRL (SRL_out, comparator_26_eq, comparator_27_eq, comparator_28_eq);
  and SRA (SRA_out, comparator_29_eq, comparator_30_eq, comparator_31_eq);
  and SLT (SLT_out, comparator_32_eq, comparator_33_eq, comparator_34_eq);
  and SLTU (SLTU_out, comparator_35_eq, comparator_36_eq, comparator_37_eq);
  and BEQ (BEQ_out, comparator_38_eq, comparator_39_eq);
  and LW_SW (LW_SW_out, comparator_40_eq, comparator_41_eq);
  or or_3 (or_3_out, or_1_out, add_out);
  assign bit_extender_1_out = {{3{1'b0}}, sub_out};  // Bit_Extender bit_extender_1
  assign bit_extender_2_out = {{3{1'b0}}, AND_out};  // Bit_Extender bit_extender_2
  assign bit_extender_3_out = {{3{1'b0}}, OR_2_out};  // Bit_Extender bit_extender_3
  assign bit_extender_4_out = {{3{1'b0}}, XOR_out};  // Bit_Extender bit_extender_4
  assign bit_extender_5_out = {{3{1'b0}}, SLL_out};  // Bit_Extender bit_extender_5
  assign bit_extender_6_out = {{3{1'b0}}, SRL_out};  // Bit_Extender bit_extender_6
  assign bit_extender_7_out = {{3{1'b0}}, SRA_out};  // Bit_Extender bit_extender_7
  assign bit_extender_8_out = {{3{1'b0}}, SLT_out};  // Bit_Extender bit_extender_8
  assign bit_extender_9_out = {{3{1'b0}}, SLTU_out};  // Bit_Extender bit_extender_9
  assign bit_extender_10_out = {{3{1'b0}}, BEQ_out};  // Bit_Extender bit_extender_10
  assign bit_extender_11_out = {{3{1'b0}}, LW_SW_out};  // Bit_Extender bit_extender_11
  assign bit_extender_12_out = {{3{1'b0}}, or_3_out};  // Bit_Extender bit_extender_12
  Multiplexer #(.select(4), .width(4), .enable("false")) multiplexer_1 (
    .in0(bit_extender_12_out), .in1(bit_extender_12_out), .in2(bit_extender_1_out), .in3(bit_extender_2_out),
    .in4(bit_extender_3_out), .in5(bit_extender_4_out), .in6(bit_extender_5_out), .in7(bit_extender_6_out),
    .in8(bit_extender_7_out), .in9(bit_extender_8_out), .in10(bit_extender_9_out),
    .in11(bit_extender_10_out), .in12(bit_extender_11_out), .in13(4'b0000), .in14(4'b0000), .in15(4'b0000),
    .out(OUTPUT), .sel(in_4));
endmodule

module DATA_MEMORY (
  input  [31:0] ADDRESS,
  input  [31:0] MMIO_INPUT,
  input  [31:0] WRITE_DATA,
  input  MEMWRITE,
  input  in_5,
  input  MEMREAD,
  output MMIO_WR,
  output [31:0] READDATA,
  output [31:0] MMIO_BYTE32
);

  wire or_1_out;

  or or_1 (or_1_out, ADDRESS[0], 1'b1);
  // Comparator #(.width(32)) comparator_1: pin names not known; wires that end beside it: ADDRESS
  // Comparator #(.width(32)) comparator_2: pin names not known; wires that end beside it: ADDRESS
  // AND_Gate and_1 has open pins: out=ADDRESS[0]
  RAM #(.dataWidth(32), .bus("separate")) ram_1 (
    .addr(ADDRESS[7:0]), .din(WRITE_DATA), .data({MMIO_INPUT[31:1], MEMREAD}), .str(ADDRESS[0]),
    .sel(or_1_out), .clk(in_5), .ld(1'b1), .clr(1'b0));
  // Multiplexer #(.width(32), .enable("false")) multiplexer_1: pin names not known; wires that end beside it: {MMIO_INPUT[31:1], MEMREAD}
  // AND_Gate and_2: pin names not known; wires that end beside it: 1'b1, {MMIO_INPUT[31:1], MEMREAD}
  // Pins of 1 and 32 bits meet at ADDRESS
  // Pins of 1 and 32 bits meet at {MMIO_INPUT[31:1], MEMREAD}

  assign MEMWRITE = ADDRESS[0];
  assign MMIO_BYTE32 = WRITE_DATA;
  assign MMIO_INPUT[0] = MEMREAD;
  assign MMIO_WR = ADDRESS[0];
  assign READDATA = {MMIO_INPUT[31:1], MEMREAD};
  // also tied to GND on the sheet: {ADDRESS[1], ADDRESS[3], ADDRESS[4], ADDRESS[5], ADDRESS[6], ADDRESS[7], ADDRESS[8], ADDRESS[9], ADDRESS[10], ADDRESS[11], ADDRESS[12], ADDRESS[13], ADDRESS[14], ADDRESS[15], ADDRESS[16], ADDRESS[17], ADDRESS[18], ADDRESS[19], ADDRESS[20], ADDRESS[21], ADDRESS[22], ADDRESS[23], ADDRESS[24], ADDRESS[25], ADDRESS[26], ADDRESS[27], ADDRESS[29], ADDRESS[30], ADDRESS[31], ADDRESS[0]}
  // also tied to VCC on the sheet: {ADDRESS[2], ADDRESS[28]}
endmodule

module ALU_With_branch (
  input  [31:0] A,
  input  [2:0] BranchType,
  input  [31:0] B,
  input  [3:0] ALUOp,
  output out_5,
  output [31:0] out_6
);

  wire comparator_1_eq, comparator_2_eq, comparator_3_eq, multiplexer_1_out, not_1_out, not_2_out, not_3_out;
  wire [31:0] adder_1_out, and_1_out, bit_extender_1_out, bit_extender_2_out, or_1_out, shifter_1_out,
       shifter_2_out, shifter_3_out, subtractor_1_out, subtractor_2_out, xor_1_out;

  // Text text_1: pin names not known
  Adder #(.width(32)) adder_1 (.a(A), .b(B), .out(adder_1_out));  // open: cin, cout
  // Text text_2: pin names not known
  Subtractor #(.width(32)) subtractor_1 (.a(A), .b(B), .out(subtractor_1_out));  // open: bin, bout
  // Text text_3: pin names not known
  // Text text_4: pin names not known
  // Text text_5: pin names not known
  // Text text_6: pin names not known
  Shifter #(.width(32)) shifter_1 (.in(A), .\dist (B[4:0]), .out(shifter_1_out));
  // Text text_7: pin names not known
  Shifter #(.width(32), .shift("lr")) shifter_2 (.in(A), .\dist (B[4:0]), .out(shifter_2_out));
  // Text text_8: pin names not known
  Shifter #(.width(32), .shift("ar")) shifter_3 (.in(A), .\dist (B[4:0]), .out(shifter_3_out));
  // Text text_9: pin names not known
  Subtractor #(.width(32)) subtractor_2 (.a(A), .b(B), .out(subtractor_2_out));  // open: bin, bout
  // Text text_10: pin names not known; wires that end beside it: B
  Comparator #(.width(32)) comparator_1 (.a(A), .b(B), .eq(comparator_1_eq));  // open: gt, lt
  assign and_1_out = A & B;  // AND_Gate and_1, 32 bits wide
  assign or_1_out = A | B;  // OR_Gate or_1, 32 bits wide
  assign xor_1_out = A ^ B;  // XOR_Gate xor_1, 32 bits wide
  Comparator #(.width(32)) comparator_2 (.a(subtractor_1_out), .b({32{1'b0}}), .eq(comparator_2_eq));  // open: gt, lt
  assign bit_extender_1_out = {{31{1'b0}}, multiplexer_1_out};  // Bit_Extender bit_extender_1
  Multiplexer #(.enable("false")) multiplexer_1 (
    .in0(1'b1), .in1(1'b0), .out(multiplexer_1_out), .sel(comparator_1_eq));
  assign bit_extender_2_out = {{31{1'b0}}, comparator_2_eq};  // Bit_Extender bit_extender_2
  Multiplexer #(.select(4), .width(32), .enable("false")) multiplexer_2 (
    .in0(adder_1_out), .in1(adder_1_out), .in2(bit_extender_2_out), .in3(subtractor_1_out), .in4(and_1_out),
    .in5(or_1_out), .in6(xor_1_out), .in7(shifter_1_out), .in8(shifter_2_out), .in9(shifter_3_out),
    .in10(subtractor_2_out), .in11(bit_extender_1_out), .in12({32{1'b0}}), .in13({32{1'b0}}),
    .in14({32{1'b0}}), .in15({32{1'b0}}), .out(out_6), .sel(ALUOp));
  Comparator #(.width(32)) comparator_3 (.a(subtractor_1_out), .b({32{1'b0}}), .eq(comparator_3_eq));  // open: gt, lt
  not not_1 (not_1_out, comparator_3_eq);
  not not_2 (not_2_out, subtractor_2_out[1]);
  Multiplexer #(.select(3), .enable("false")) multiplexer_3 (
    .in0(comparator_3_eq), .in1(not_1_out), .in2(subtractor_2_out[1]), .in3(not_2_out),
    .in4(multiplexer_1_out), .in5(not_3_out), .in6(1'b0), .in7(1'b0), .out(out_5), .sel(BranchType));
  not not_3 (not_3_out, multiplexer_1_out);
endmodule

module Unique_Register (
  input  [4:0] in_1,
  input  [4:0] in_2,
  input  in_3,
  input  in_4,
  input  [4:0] in_5,
  output [31:0] out_6,
  output [31:0] out_7
);

  wire and_1_out, clock_1_out, comparator_1_eq, comparator_2_eq, not_1_out;
  wire [4:0] multiplexer_1_out;
  wire [31:0] bit_extender_1_out, ram_1_data;

  // Text text_1: pin names not known
  // Text text_2: pin names not known
  // Text text_3: pin names not known
  // Text text_4: pin names not known
  Clock clock_1 (.out(clock_1_out));
  // Text text_5: pin names not known
  Multiplexer #(.width(5), .enable("false")) multiplexer_1 (
    .in0(in_1), .in1(in_2), .out(multiplexer_1_out), .sel(in_3));
  assign bit_extender_1_out = {{27{1'b0}}, in_5};  // Bit_Extender bit_extender_1
  Comparator #(.width(5)) comparator_1 (.a(in_2), .b({5{1'b0}}), .eq(comparator_1_eq));  // open: gt, lt
  RAM #(.addrWidth(5), .dataWidth(32)) ram_1 (
    .addr(in_5), .data(ram_1_data), .sel(1'b1), .clk(clock_1_out), .ld(1'b0), .clr(in_4));
  Comparator #(.width(32)) comparator_2 (.a(bit_extender_1_out), .b({32{1'b0}}), .eq(comparator_2_eq));  // open: gt, lt
  not not_1 (not_1_out, comparator_1_eq);
  // Text text_6: pin names not known
  and and_1 (and_1_out, not_1_out, in_3);
  RAM #(.addrWidth(5), .dataWidth(32)) ram_2 (
    .addr(multiplexer_1_out), .data(out_6), .sel(1'b1), .clk(clock_1_out), .ld(and_1_out), .clr(in_4));
  Multiplexer #(.width(32), .enable("false")) multiplexer_2 (
    .in0(32'ha5a5a5a5), .in1(ram_1_data), .out(out_7), .sel(comparator_2_eq));
  // Text text_7: pin names not known
  // Text text_8: pin names not known; wires that end beside it: 32'ha5a5a5a5
endmodule

module Program_counter (
  input  [31:0] in_1,
  input  [31:0] in_2,
  input  in_3,
  input  in_4,
  input  in_5
);

  wire [31:0] register_1_q;

  Register #(.width(32)) register_1 (.D(in_1), .en(in_3), .Q(register_1_q), .clk(in_4), .clr(in_5));
  RAM #(.addrWidth(24), .dataWidth(32)) ram_1 (
    .addr(register_1_q[25:2]), .data(in_2), .sel(in_3), .clk(in_4), .clr(in_5));  // open: ld
endmodule

module draft (
  input  in_1,
  input  in_2,
  input  [2:0] FUNCT_3,
  input  [2:0] in_4,
  output [2:0] out_5,
  output [3:0] OUTPUT
);

  wire add_out, AND_out, BEQ_out, comparator_1_eq, comparator_2_eq, comparator_3_eq, comparator_4_eq,
       comparator_5_eq, comparator_6_eq, comparator_7_eq, comparator_8_eq, comparator_9_eq, comparator_10_eq,
       comparator_11_eq, comparator_12_eq, comparator_13_eq, comparator_14_eq, comparator_15_eq,
       comparator_16_eq, comparator_17_eq, comparator_18_eq, LW_SW_out, OR_out, SLT_out, sub_out, undriven_4,
       XOR_out;
  wire [2:0] undriven_6;
  wire [6:0] instruction_decoder_1_out_2, undriven, undriven_2;
  wire [31:0] undriven_3, undriven_5;

  Program_counter program_counter_1 (.in_1(undriven_3), .in_3(in_1), .in_4(undriven_4), .in_5(in_2), .in_2(undriven_5));
  Clock clock_1 ();  // open: out
  instruction_decoder instruction_decoder_1 (
    .in_1(undriven_5), .out_2(instruction_decoder_1_out_2));  // open: out_3, out_4, out_5, out_6, out_7
  Comparator #(.width(7)) comparator_1 (.a(undriven_2), .b(7'b0110011), .eq(comparator_1_eq));  // open: gt, lt
  Comparator #(.width(3)) comparator_2 (.a(FUNCT_3), .b(3'b000), .eq(comparator_2_eq));  // open: gt, lt
  Comparator #(.width(7)) comparator_3 (.a(undriven), .b({7{1'b0}}), .eq(comparator_3_eq));  // open: gt, lt
  Comparator #(.width(7)) comparator_4 (.a(undriven_2), .b(7'b0110011), .eq(comparator_4_eq));  // open: gt, lt
  Comparator #(.width(3)) comparator_5 (.a(FUNCT_3), .b(3'b000), .eq(comparator_5_eq));  // open: gt, lt
  Comparator #(.width(7)) comparator_6 (.a(undriven), .b(7'b0100000), .eq(comparator_6_eq));  // open: gt, lt
  Comparator #(.width(7)) comparator_7 (.a(undriven_2), .b(7'b0110011), .eq(comparator_7_eq));  // open: gt, lt
  Comparator #(.width(3)) comparator_8 (.a(FUNCT_3), .b(3'b111), .eq(comparator_8_eq));  // open: gt, lt
  Comparator #(.width(7)) comparator_9 (.a(undriven_2), .b(7'b0110011), .eq(comparator_9_eq));  // open: gt, lt
  Comparator #(.width(3)) comparator_10 (.a(FUNCT_3), .b(3'b110), .eq(comparator_10_eq));  // open: gt, lt
  Comparator #(.width(7)) comparator_11 (.a(undriven_2), .b(7'b0110011), .eq(comparator_11_eq));  // open: gt, lt
  Comparator #(.width(3)) comparator_12 (.a(FUNCT_3), .b(3'b010), .eq(comparator_12_eq));  // open: gt, lt
  Comparator #(.width(7)) comparator_13 (.a(undriven_2), .b(7'b0110011), .eq(comparator_13_eq));  // open: gt, lt
  Comparator #(.width(3)) comparator_14 (.a(FUNCT_3), .b(3'b100), .eq(comparator_14_eq));  // open: gt, lt
  Comparator #(.width(7)) comparator_15 (.a(undriven_2), .b(7'b1100011), .eq(comparator_15_eq));  // open: gt, lt
  Comparator #(.width(3)) comparator_16 (.a(FUNCT_3), .b(3'b000), .eq(comparator_16_eq));  // open: gt, lt
  // Text text_1: pin names not known
  Comparator #(.width(7)) comparator_17 (.a(undriven_2), .b(7'b0000011), .eq(comparator_17_eq));  // open: gt, lt
  Comparator #(.width(7)) comparator_18 (.a(undriven_2), .b(7'b0100011), .eq(comparator_18_eq));  // open: gt, lt
  control_decode control_decode (.in_1(instruction_decoder_1_out_2));  // open: out_2, out_3, out_4, out_5, out_6, out_7, out_8, out_9
  and add (add_out, comparator_1_eq, comparator_2_eq, comparator_3_eq);
  and sub (sub_out, comparator_4_eq, comparator_5_eq, comparator_6_eq);
  and AND (AND_out, comparator_7_eq, comparator_8_eq);
  and OR (OR_out, comparator_9_eq, comparator_10_eq);
  and SLT (SLT_out, comparator_11_eq, comparator_12_eq);
  and XOR (XOR_out, comparator_13_eq, comparator_14_eq);
  and BEQ (BEQ_out, comparator_15_eq, comparator_16_eq);
  and LW_SW (LW_SW_out, comparator_17_eq, comparator_18_eq);
  Decoder #(.select(3), .enable("false")) decoder_1 (
    .out0(add_out), .out1(sub_out), .out2(AND_out), .out3(OR_out), .out4(SLT_out), .out5(XOR_out),
    .out6(BEQ_out), .out7(LW_SW_out), .sel(in_4));
  Bit_Extender #(.in_width(1), .out_width(3)) bit_extender_1 (.out(out_5));  // open: in
  Multiplexer #(.select(3), .width(4), .enable("false")) multiplexer_1 (
    .in0(4'b0010), .in1(4'b0110), .in2(4'b0000), .in3(4'b0001), .in4(4'b0111), .in5(4'b0011), .in6(4'b0110),
    .in7(4'b0010), .out(OUTPUT), .sel(undriven_6));
endmodule

module draft_1 (
  input  [31:0] MMIO_INPUT,
  input  in_2,
  input  in_3,
  input  [31:0] WriteData,
  input  in_5,
  input  [4:0] ReadReg1,
  input  in_7,
  input  [4:0] WriteReg,
  input  [4:0] ReadReg2,
  output out_10,
  output SW0,
  output SW4,
  output SW1,
  output SW5,
  output SW2,
  output SW6,
  output SW3,
  output SW7,
  output STROBE,
  output [31:0] Read_Data1,
  output out_21,
  output [1:0] out_22,
  output out_23,
  output [31:0] Read_Data2,
  output out_25,
  output out_26,
  output [2:0] out_27,
  output out_28
);

  wire ALU_With_Branch_out_5, and_1_out, and_2_out, clock_1_out, clock_2_out, comparator_1_eq,
       comparator_2_eq, comparator_3_eq, comparator_4_eq, comparator_5_eq, comparator_6_eq, comparator_7_eq,
       comparator_8_eq, comparator_9_eq, comparator_13_eq, control_decode_out_2, control_decode_out_3,
       control_decode_out_5, control_decode_out_6, control_decode_out_7, control_decode_out_9,
       decoder_1_out0, decoder_1_out1, decoder_1_out2, decoder_1_out3, decoder_1_out4, decoder_1_out5,
       decoder_1_out6, decoder_1_out7, decoder_1_out8, decoder_1_out9, decoder_1_out10, decoder_1_out11,
       decoder_1_out12, decoder_1_out13, decoder_1_out14, decoder_1_out15, decoder_1_out16, decoder_1_out17,
       decoder_1_out18, decoder_1_out19, decoder_1_out20, decoder_1_out21, decoder_1_out22, decoder_1_out23,
       decoder_1_out24, decoder_1_out25, decoder_1_out26, decoder_1_out27, decoder_1_out28, decoder_1_out29,
       decoder_1_out30, decoder_1_out31, or_1_out, or_3_out, or_5_out;
  wire [1:0] bit_extender_2_out, bit_extender_3_out;
  wire [2:0] priority_encoder_1_out;
  wire [3:0] ALUControl_output;
  wire [6:0] ram_1_data;
  wire [7:0] control_decode_out_8;
  wire [31:0] adder_1_out, adder_2_out, ALU_With_Branch_out_6, Data_memory_p6, immediate_gen_out_4,
       multiplexer_1_out, multiplexer_3_out, multiplexer_4_out, R0_q, R1_q, R2_q, R3_q, R4_q, R5_q, R6_q,
       R7_q, R8_q, R9_q, R10_q, R11_q, R12_q, R13_q, R14_q, R15_q, R16_q, R17_q, R18_q, R19_q, R20_q, R21_q,
       R22_q, R23_q, R24_q, R25_q, R26_q, R27_q, R28_q, R29_q, R30_q, R31_q, ram_2_data, register_1_q,
       register_2_q, Register_file_p1, Register_file_p7, Register_file_p8, undriven, undriven_2;
  wire [31:7] ram_1_data_2;

  Priority_Encoder priority_encoder_1 (
    .out(priority_encoder_1_out), .en_in(1'b1), .gs(out_10));  // open: in0, in1, in2, in3, in4, in5, in6, in7, en_out
  Register #(.width(32)) register_1 (.D(multiplexer_3_out), .en(in_2), .Q(register_1_q), .clk(clock_1_out), .clr(in_3));
  Clock clock_1 (.out(clock_1_out));
  Register #(.width(32)) register_2 (.D(undriven), .en(in_5), .Q(register_2_q), .clk(clock_2_out), .clr(in_7));
  Clock clock_2 (.out(clock_2_out));
  control_decode control_decode (
    .in_1(ram_1_data), .out_2(control_decode_out_2), .out_3(control_decode_out_3),
    .out_5(control_decode_out_5), .out_6(control_decode_out_6), .out_7(control_decode_out_7),
    .out_8(control_decode_out_8[0]), .out_9(control_decode_out_9));  // open: out_4
  RAM #(.addrWidth(24), .dataWidth(32)) ram_1 (
    .addr(register_1_q[25:2]), .data({ram_1_data_2, ram_1_data}), .sel(in_2), .clk(clock_1_out), .clr(in_3));  // open: ld
  RAM #(.addrWidth(24), .dataWidth(32)) ram_2 (
    .addr(register_2_q[25:2]), .data(ram_2_data), .sel(in_5), .clk(clock_2_out), .clr(in_7));  // open: ld
  immediate_generation immediate_gen (
    .in_1({ram_1_data_2, ram_1_data}), .out_4(immediate_gen_out_4));  // open: in_2, in_3
  // Register_File Register_file: pin names not known; wires that end beside it: Register_file_p1, clock_1_out, control_decode_out_2, ram_1_data_2[11:7], ram_1_data_2[19:15], ram_1_data_2[24:20], Register_file_p7, Register_file_p8
  ALU_CONTROL ALUControl (
    .OPCODE(ram_1_data), .FUNCT_3(ram_1_data_2[14:12]), .FUNCT_7(ram_1_data_2[31:25]),
    .OUTPUT(ALUControl_output));  // open: in_4
  // Text text_1: pin names not known
  Multiplexer #(.width(32), .enable("false")) multiplexer_1 (
    .in0(Register_file_p8), .in1(immediate_gen_out_4), .out(multiplexer_1_out), .sel(control_decode_out_3));
  Comparator #(.width(7)) comparator_1 (.a(ram_2_data[6:0]), .b(7'b0110011), .eq(comparator_1_eq));  // open: gt, lt
  Comparator #(.width(7)) comparator_2 (.a(ram_2_data[6:0]), .b(7'b0010011), .eq(comparator_2_eq));  // open: gt, lt
  Comparator #(.width(7)) comparator_3 (.a(ram_2_data[6:0]), .b(7'b0000011), .eq(comparator_3_eq));  // open: gt, lt
  Comparator #(.width(7)) comparator_4 (.a(ram_2_data[6:0]), .b(7'b1101111), .eq(comparator_4_eq));  // open: gt, lt
  Comparator #(.width(7)) comparator_5 (.a(ram_2_data[6:0]), .b(7'b0010011), .eq(comparator_5_eq));  // open: gt, lt
  Comparator #(.width(7)) comparator_6 (.a(ram_2_data[6:0]), .b(7'b0000011), .eq(comparator_6_eq));  // open: gt, lt
  Comparator #(.width(7)) comparator_7 (.a(ram_2_data[6:0]), .b(7'b0100011), .eq(comparator_7_eq));  // open: gt, lt
  Comparator #(.width(7)) comparator_8 (.a(ram_2_data[6:0]), .b(7'b0110011), .eq(comparator_8_eq));  // open: gt, lt
  Comparator #(.width(7)) comparator_9 (.a(ram_2_data[6:0]), .b(7'b1100011), .eq(comparator_9_eq));  // open: gt, lt
  Comparator #(.width(7)) comparator_10 (.a(ram_2_data[6:0]), .b(7'b0000011), .eq(out_23));  // open: gt, lt
  Comparator #(.width(7)) comparator_11 (.a(ram_2_data[6:0]), .b(7'b0100011), .eq(out_25));  // open: gt, lt
  Comparator #(.width(7)) comparator_12 (.a(ram_2_data[6:0]), .b(7'b0000011), .eq(out_26));  // open: gt, lt
  Comparator #(.width(7)) comparator_13 (.a(ram_2_data[6:0]), .b(7'b1100011), .eq(comparator_13_eq));  // open: gt, lt
  Comparator #(.width(7)) comparator_14 (.a(ram_2_data[6:0]), .b(7'b1101111), .eq(out_28));  // open: gt, lt
  // Text text_2: pin names not known; wires that end beside it: SW0, SW1, SW2, SW3, SW4, SW5, SW6, SW7, MMIO_INPUT
  ALU_With_branch ALU_With_Branch (
    .A(Register_file_p7), .B(multiplexer_1_out), .ALUOp(ALUControl_output),
    .BranchType(control_decode_out_8[2:0]), .out_5(ALU_With_Branch_out_5), .out_6(ALU_With_Branch_out_6));
  // Probe on ALU_With_Branch_out_6
  // Register #(.width(32)) MMIO_LATCH: pin names not known; wires that end beside it: STROBE
  assign out_27 = {{2{1'b0}}, comparator_13_eq};  // Bit_Extender bit_extender_1
  // DATA_MEMORY Data_memory: pin names not known; wires that end beside it: ALU_With_Branch_out_6, Register_file_p8, clock_1_out, control_decode_out_6, control_decode_out_5, Data_memory_p6
  and and_1 (and_1_out, control_decode_out_8[2], ALU_With_Branch_out_5);
  // Text text_3: pin names not known
  or or_1 (or_1_out, comparator_1_eq, comparator_2_eq, comparator_3_eq, comparator_4_eq);
  // Text text_4: pin names not known
  or or_2 (out_21, comparator_5_eq, comparator_6_eq, comparator_7_eq);
  assign bit_extender_2_out = {{1{1'b0}}, comparator_8_eq};  // Bit_Extender bit_extender_2
  assign bit_extender_3_out = {{1{1'b0}}, comparator_9_eq};  // Bit_Extender bit_extender_3
  // Text text_5: pin names not known
  // Text text_6: pin names not known
  Multiplexer #(.width(32), .enable("false")) multiplexer_2 (
    .in0(ALU_With_Branch_out_6), .in1(Data_memory_p6), .out(Register_file_p1), .sel(control_decode_out_7));
  // Probe on Data_memory_p6
  // Text text_7: pin names not known
  or or_3 (or_3_out, control_decode_out_7, and_1_out);
  // Text text_8: pin names not known
  // Text text_9: pin names not known
  // Text text_10: pin names not known
  // Text text_11: pin names not known
  // Text text_12: pin names not known
  // Probe on Data_memory_p6
  // Text text_13: pin names not known
  assign out_22 = bit_extender_2_out | bit_extender_3_out;  // OR_Gate or_4, 2 bits wide
  Adder #(.width(32)) adder_1 (.a(32'h4), .b(register_1_q), .out(adder_1_out));  // open: cin, cout
  // Probe on Data_memory_p6
  // Probe on Data_memory_p6
  // Probe on Data_memory_p6
  // Probe on Data_memory_p6
  // Probe on Data_memory_p6
  // Probe on Data_memory_p6
  Adder #(.width(32)) adder_2 (.a(register_1_q), .b(immediate_gen_out_4), .out(adder_2_out));  // open: cin, cout
  // Probe on Data_memory_p6
  // Text text_14: pin names not known
  Multiplexer #(.width(32), .enable("false")) multiplexer_3 (
    .in0(adder_1_out), .in1(adder_2_out), .out(multiplexer_3_out), .sel(or_5_out));
  or or_5 (or_5_out, or_3_out, control_decode_out_9);
  Decoder #(.select(5), .enable("false")) decoder_1 (
    .out0(decoder_1_out0), .out1(decoder_1_out1), .out2(decoder_1_out2), .out3(decoder_1_out3),
    .out4(decoder_1_out4), .out5(decoder_1_out5), .out6(decoder_1_out6), .out7(decoder_1_out7),
    .out8(decoder_1_out8), .out9(decoder_1_out9), .out10(decoder_1_out10), .out11(decoder_1_out11),
    .out12(decoder_1_out12), .out13(decoder_1_out13), .out14(decoder_1_out14), .out15(decoder_1_out15),
    .out16(decoder_1_out16), .out17(decoder_1_out17), .out18(decoder_1_out18), .out19(decoder_1_out19),
    .out20(decoder_1_out20), .out21(decoder_1_out21), .out22(decoder_1_out22), .out23(decoder_1_out23),
    .out24(decoder_1_out24), .out25(decoder_1_out25), .out26(decoder_1_out26), .out27(decoder_1_out27),
    .out28(decoder_1_out28), .out29(decoder_1_out29), .out30(decoder_1_out30), .out31(decoder_1_out31),
    .sel(WriteReg));
  and and_2 (and_2_out, 1'b0, decoder_1_out0);
  Multiplexer #(.width(32), .enable("false")) multiplexer_4 (
    .in0(undriven_2), .in1(WriteData), .out(multiplexer_4_out), .sel(or_1_out));
  Register #(.width(32)) R0 (.D(multiplexer_4_out), .en(and_2_out), .Q(R0_q), .clk(clock_2_out));  // open: clr
  Register #(.width(32)) R1 (.D(multiplexer_4_out), .en(decoder_1_out1), .Q(R1_q), .clk(clock_2_out));  // open: clr
  Register #(.width(32)) R8 (.D(multiplexer_4_out), .en(decoder_1_out8), .Q(R8_q), .clk(clock_2_out));  // open: clr
  Register #(.width(32)) R2 (.D(multiplexer_4_out), .en(decoder_1_out2), .Q(R2_q), .clk(clock_2_out));  // open: clr
  Register #(.width(32)) R9 (.D(multiplexer_4_out), .en(decoder_1_out9), .Q(R9_q), .clk(clock_2_out));  // open: clr
  Register #(.width(32)) R16 (.D(multiplexer_4_out), .en(decoder_1_out16), .Q(R16_q), .clk(clock_2_out));  // open: clr
  Register #(.width(32)) R3 (.D(multiplexer_4_out), .en(decoder_1_out3), .Q(R3_q), .clk(clock_2_out));  // open: clr
  Register #(.width(32)) R4 (.D(multiplexer_4_out), .en(decoder_1_out4), .Q(R4_q), .clk(clock_2_out));  // open: clr
  Register #(.width(32)) R10 (.D(multiplexer_4_out), .en(decoder_1_out10), .Q(R10_q), .clk(clock_2_out));  // open: clr
  Register #(.width(32)) R17 (.D(multiplexer_4_out), .en(decoder_1_out17), .Q(R17_q), .clk(clock_2_out));  // open: clr
  Register #(.width(32)) R24 (.D(multiplexer_4_out), .en(decoder_1_out24), .Q(R24_q), .clk(clock_2_out));  // open: clr
  Register #(.width(32)) R5 (.D(multiplexer_4_out), .en(decoder_1_out5), .Q(R5_q), .clk(clock_2_out));  // open: clr
  Register #(.width(32)) R12 (.D(multiplexer_4_out), .en(decoder_1_out12), .Q(R12_q), .clk(clock_2_out));  // open: clr
  Register #(.width(32)) R11 (.D(multiplexer_4_out), .en(decoder_1_out11), .Q(R11_q), .clk(clock_2_out));  // open: clr
  Register #(.width(32)) R18 (.D(multiplexer_4_out), .en(decoder_1_out18), .Q(R18_q), .clk(clock_2_out));  // open: clr
  Register #(.width(32)) R25 (.D(multiplexer_4_out), .en(decoder_1_out25), .Q(R25_q), .clk(clock_2_out));  // open: clr
  Register #(.width(32)) R26 (.D(multiplexer_4_out), .en(decoder_1_out26), .Q(R26_q), .clk(clock_2_out));  // open: clr
  Register #(.width(32)) R6 (.D(multiplexer_4_out), .en(decoder_1_out6), .Q(R6_q), .clk(clock_2_out));  // open: clr
  Register #(.width(32)) R13 (.D(multiplexer_4_out), .en(decoder_1_out13), .Q(R13_q), .clk(clock_2_out));  // open: clr
  Register #(.width(32)) R19 (.D(multiplexer_4_out), .en(decoder_1_out19), .Q(R19_q), .clk(clock_2_out));  // open: clr
  Register #(.width(32)) R20 (.D(multiplexer_4_out), .en(decoder_1_out20), .Q(R20_q), .clk(clock_2_out));  // open: clr
  Register #(.width(32)) R27 (.D(multiplexer_4_out), .en(decoder_1_out27), .Q(R27_q), .clk(clock_2_out));  // open: clr
  Register #(.width(32)) R7 (.D(multiplexer_4_out), .en(decoder_1_out7), .Q(R7_q), .clk(clock_2_out));  // open: clr
  Register #(.width(32)) R14 (.D(multiplexer_4_out), .en(decoder_1_out14), .Q(R14_q), .clk(clock_2_out));  // open: clr
  Register #(.width(32)) R21 (.D(multiplexer_4_out), .en(decoder_1_out21), .Q(R21_q), .clk(clock_2_out));  // open: clr
  Register #(.width(32)) R28 (.D(multiplexer_4_out), .en(decoder_1_out28), .Q(R28_q), .clk(clock_2_out));  // open: clr
  Register #(.width(32), .trigger("falling")) R15 (
    .D(multiplexer_4_out), .en(decoder_1_out15), .Q(R15_q), .clk(clock_2_out));  // open: clr
  Register #(.width(32)) R22 (.D(multiplexer_4_out), .en(decoder_1_out22), .Q(R22_q), .clk(clock_2_out));  // open: clr
  Register #(.width(32)) R29 (.D(multiplexer_4_out), .en(decoder_1_out29), .Q(R29_q), .clk(clock_2_out));  // open: clr
  Register #(.width(32)) R23 (.D(multiplexer_4_out), .en(decoder_1_out23), .Q(R23_q), .clk(clock_2_out));  // open: clr
  Register #(.width(32)) R30 (.D(multiplexer_4_out), .en(decoder_1_out30), .Q(R30_q), .clk(clock_2_out));  // open: clr
  Register #(.width(32)) R31 (.D(multiplexer_4_out), .en(decoder_1_out31), .Q(R31_q), .clk(clock_2_out));  // open: clr
  Multiplexer #(.select(5), .width(32), .enable("false")) multiplexer_5 (
    .in0(R0_q), .in1(R1_q), .in2(R2_q), .in3(R3_q), .in4(R4_q), .in5(R5_q), .in6(R6_q), .in7(R7_q),
    .in8(R8_q), .in9(R9_q), .in10(R10_q), .in11(R11_q), .in12(R12_q), .in13(R13_q), .in14(R14_q),
    .in15(R15_q), .in16(R16_q), .in17(R17_q), .in18(R18_q), .in19(R19_q), .in20(R20_q), .in21(R21_q),
    .in22(R22_q), .in23(R23_q), .in24(R24_q), .in25(R25_q), .in26(R26_q), .in27(R27_q), .in28(R28_q),
    .in29(R29_q), .in30(R30_q), .in31(R31_q), .out(Read_Data1), .sel(ReadReg1));
  Multiplexer #(.select(5), .width(32), .enable("false")) multiplexer_6 (
    .in0(R0_q), .in1(R1_q), .in2(R2_q), .in3(R3_q), .in4(R4_q), .in5(R5_q), .in6(R6_q), .in7(R7_q),
    .in8(R8_q), .in9(R9_q), .in10(R10_q), .in11(R11_q), .in12(R12_q), .in13(R13_q), .in14(R14_q),
    .in15(R15_q), .in16(R16_q), .in17(R17_q), .in18(R18_q), .in19(R19_q), .in20(R20_q), .in21(R21_q),
    .in22(R22_q), .in23(R23_q), .in24(R24_q), .in25(R25_q), .in26(R26_q), .in27(R27_q), .in28(R28_q),
    .in29(R29_q), .in30(R30_q), .in31(R31_q), .out(Read_Data2), .sel(ReadReg2));
  // Pins of 1 and 3 and 8 bits meet at control_decode_out_8
endmodule

module draft_main_x (
  input  [6:0] in_1,
  input  [6:0] FUNCT_7,
  input  [2:0] FUNCT_3,
  input  in_4,
  input  in_5,
  input  [3:0] in_6,
  input  in_7,
  input  in_8,
  input  [4:0] in_9,
  input  [4:0] in_10,
  input  in_11,
  input  in_12,
  input  [4:0] in_13,
  output [31:0] out_14,
  output [31:0] out_15
);

  wire add_out, ALU_With_Branch_out_5, and_1_out, and_2_out, AND_3_out, BEQ_out, clock_1_out, clock_2_out,
       clock_3_out, comparator_1_eq, comparator_2_eq, comparator_4_eq, comparator_6_eq, comparator_7_eq,
       comparator_8_eq, comparator_10_eq, comparator_12_eq, comparator_13_eq, comparator_14_eq,
       comparator_15_eq, comparator_16_eq, comparator_17_eq, comparator_18_eq, comparator_19_eq,
       comparator_20_eq, comparator_21_eq, comparator_22_eq, comparator_23_eq, comparator_24_eq,
       comparator_25_eq, comparator_26_eq, comparator_27_eq, comparator_28_eq, comparator_29_eq,
       comparator_30_eq, control_decode_out_2, control_decode_out_3, control_decode_out_5,
       control_decode_out_6, control_decode_out_7, control_decode_out_9, LW_SW_out, not_1_out, or_1_out,
       or_2_out, or_3_out, OR_4_out, SLT_out, sub_out, text_10_p1, text_12_p1, text_16_p1, text_18_p1,
       XOR_out;
  wire [2:0] control_decode_out_8, ram_2_data_3;
  wire [3:0] ALUControl_output, bit_extender_2_out, bit_extender_3_out, bit_extender_4_out,
       bit_extender_5_out, bit_extender_6_out, bit_extender_7_out, bit_extender_8_out, bit_extender_9_out,
       multiplexer_6_out;
  wire [4:0] multiplexer_1_out, ram_2_data_2, ram_2_data_4, ram_2_data_5;
  wire [6:0] Instruction_Decoder_out_2, ram_2_data, undriven_3, undriven_4;
  wire [31:0] adder_1_out, adder_2_out, adder_3_out, ALU_With_Branch_out_6, bit_extender_1_out,
       Data_memory_p6, immediate_gen_out_4, multiplexer_3_out, multiplexer_5_out, ram_1_data, ram_3_data,
       register_1_q, register_2_q, Register_file_p1, Register_file_p7, Register_file_p8, undriven, undriven_2;
  wire [31:25] ram_2_data_6;

  Clock clock_1 (.out(clock_1_out));
  Register #(.width(32)) register_1 (.D(undriven_2), .en(in_4), .Q(register_1_q), .clk(clock_1_out), .clr(in_5));
  Adder #(.width(32)) adder_1 (.a(undriven), .b(32'h4), .out(adder_1_out));  // open: cin, cout
  Clock clock_2 (.out(clock_2_out));
  Register #(.width(32)) register_2 (.D(multiplexer_5_out), .en(in_7), .Q(register_2_q), .clk(clock_2_out), .clr(in_8));
  // Text text_1: pin names not known
  // Text text_2: pin names not known
  // Text text_3: pin names not known
  // Text text_4: pin names not known
  Clock clock_3 (.out(clock_3_out));
  // Text text_5: pin names not known
  assign bit_extender_1_out = {{27{1'b0}}, in_13};  // Bit_Extender bit_extender_1
  RAM #(.addrWidth(24), .dataWidth(32)) ram_1 (
    .addr(register_1_q[25:2]), .data(ram_1_data), .sel(in_4), .clk(clock_1_out), .clr(in_5));  // open: ld
  Type_decoder Type_Decoder ();  // open: OP_CODE, out_2, out_3
  Multiplexer #(.width(5), .enable("false")) multiplexer_1 (
    .in0(in_9), .in1(in_10), .out(multiplexer_1_out), .sel(in_11));
  instruction_decoder Instruction_Decoder (
    .in_1(ram_1_data), .out_2(Instruction_Decoder_out_2));  // open: out_3, out_4, out_5, out_6, out_7
  control_decode control_decode (
    .in_1(ram_2_data), .out_2(control_decode_out_2), .out_3(control_decode_out_3),
    .out_5(control_decode_out_5), .out_6(control_decode_out_6), .out_7(control_decode_out_7),
    .out_8(control_decode_out_8[0]), .out_9(control_decode_out_9));  // open: out_4
  RAM #(.addrWidth(24), .dataWidth(32)) ram_2 (
    .addr(register_2_q[25:2]),
    .data({ram_2_data_6, ram_2_data_5, ram_2_data_4, ram_2_data_3, ram_2_data_2, ram_2_data}), .sel(in_7),
    .clk(clock_2_out), .clr(in_8));  // open: ld
  Comparator #(.width(5)) comparator_1 (.a(in_10), .b({5{1'b0}}), .eq(comparator_1_eq));  // open: gt, lt
  not not_1 (not_1_out, comparator_1_eq);
  RAM #(.addrWidth(5), .dataWidth(32)) ram_3 (
    .addr(in_13), .data(ram_3_data), .sel(1'b1), .clk(clock_3_out), .ld(1'b0), .clr(in_12));
  Comparator #(.width(32)) comparator_2 (.a(bit_extender_1_out), .b({32{1'b0}}), .eq(comparator_2_eq));  // open: gt, lt
  immediate_generation immediate_gen (
    .in_1({ram_2_data_6, ram_2_data_5, ram_2_data_4, ram_2_data_3, ram_2_data_2, ram_2_data}),
    .out_4(immediate_gen_out_4));  // open: in_2, in_3
  and and_1 (and_1_out, not_1_out, in_11);
  Type_decoder type_decoder_2 ();  // open: OP_CODE, out_2, out_3
  // Text text_6: pin names not known
  Multiplexer #(.width(32), .enable("false")) multiplexer_2 (
    .in0(32'ha5a5a5a5), .in1(ram_3_data), .out(out_15), .sel(comparator_2_eq));
  // Register_File Register_file: pin names not known; wires that end beside it: Register_file_p1, clock_2_out, control_decode_out_2, ram_2_data_2, ram_2_data_4, ram_2_data_5, Register_file_p7, Register_file_p8
  RAM #(.addrWidth(5), .dataWidth(32)) ram_4 (
    .addr(multiplexer_1_out), .data(out_14), .sel(1'b1), .clk(clock_3_out), .ld(and_1_out), .clr(in_12));
  // Text text_7: pin names not known
  // Text text_8: pin names not known; wires that end beside it: 32'ha5a5a5a5
  ALU_CONTROL ALUControl (
    .OPCODE(ram_2_data), .FUNCT_3(ram_2_data_3), .FUNCT_7(ram_2_data_6), .OUTPUT(ALUControl_output));  // open: in_4
  // Text text_9: pin names not known
  // Text text_10: pin names not known; wires that end beside it: text_10_p1
  // Text text_11: pin names not known
  // Text text_12: pin names not known; wires that end beside it: text_12_p1
  // Text text_13: pin names not known
  // Text text_14: pin names not known
  // Text text_15: pin names not known
  // Text text_16: pin names not known; wires that end beside it: text_16_p1
  // Text text_17: pin names not known
  // Text text_18: pin names not known; wires that end beside it: text_18_p1
  Multiplexer #(.width(32), .enable("false")) multiplexer_3 (
    .in0(Register_file_p8), .in1(immediate_gen_out_4), .out(multiplexer_3_out), .sel(control_decode_out_3));
  Comparator #(.width(7)) comparator_3 (.a(in_1), .b(7'b0110011), .eq(text_10_p1));  // open: gt, lt
  Comparator #(.width(7)) comparator_4 (.a(in_1), .b(7'b0010011), .eq(comparator_4_eq));  // open: gt, lt
  Comparator #(.width(7)) comparator_5 (.a(in_1), .b(7'b0000011), .eq(text_12_p1));  // open: gt, lt
  Comparator #(.width(7)) comparator_6 (.a(in_1), .b(7'b0100011), .eq(comparator_6_eq));  // open: gt, lt
  Comparator #(.width(7)) comparator_7 (.a(in_1), .b(7'b1100011), .eq(comparator_7_eq));  // open: gt, lt
  Comparator #(.width(7)) comparator_8 (.a(in_1), .b(7'b1101111), .eq(comparator_8_eq));  // open: gt, lt
  Comparator #(.width(7)) comparator_9 (.a(in_1), .b(7'b1100111), .eq(text_16_p1));  // open: gt, lt
  Comparator #(.width(7)) comparator_10 (.a(in_1), .b(7'b0110111), .eq(comparator_10_eq));  // open: gt, lt
  Comparator #(.width(7)) comparator_11 (.a(in_1), .b(7'b0010111), .eq(text_18_p1));  // open: gt, lt
  ALU_With_branch ALU_With_Branch (
    .A(Register_file_p7), .B(multiplexer_3_out), .ALUOp(ALUControl_output),
    .BranchType(control_decode_out_8), .out_5(ALU_With_Branch_out_5), .out_6(ALU_With_Branch_out_6));
  // DATA_MEMORY Data_memory: pin names not known; wires that end beside it: ALU_With_Branch_out_6, Register_file_p8, clock_2_out, control_decode_out_6, control_decode_out_5, Data_memory_p6
  and and_2 (and_2_out, control_decode_out_8[2], ALU_With_Branch_out_5);
  Multiplexer #(.width(32), .enable("false")) multiplexer_4 (
    .in0(ALU_With_Branch_out_6), .in1(Data_memory_p6), .out(Register_file_p1), .sel(control_decode_out_7));
  // Text text_19: pin names not known
  or or_1 (or_1_out, control_decode_out_7, and_2_out);
  // OR_Gate T0 has open pins: in0=comparator_4_eq, in1=comparator_7_eq, in2=comparator_8_eq, out=open
  // OR_Gate T1 has open pins: in0=comparator_7_eq, in1=comparator_6_eq, in2=comparator_10_eq, out=open
  // OR_Gate T2 has open pins: in0=comparator_10_eq, in1=comparator_8_eq, out=open
  Adder #(.width(32)) adder_2 (.a(32'h4), .b(register_2_q), .out(adder_2_out));  // open: cin, cout
  Adder #(.width(32)) adder_3 (.a(register_2_q), .b(immediate_gen_out_4), .out(adder_3_out));  // open: cin, cout
  // Text text_20: pin names not known
  or or_2 (or_2_out, or_1_out, control_decode_out_9);
  Multiplexer #(.width(32), .enable("false")) multiplexer_5 (
    .in0(adder_2_out), .in1(adder_3_out), .out(multiplexer_5_out), .sel(or_2_out));
  Comparator #(.width(7)) comparator_12 (.a(undriven_4), .b(7'b0110011), .eq(comparator_12_eq));  // open: gt, lt
  Comparator #(.width(7)) comparator_13 (.a(undriven_4), .b(7'b0010011), .eq(comparator_13_eq));  // open: gt, lt
  Comparator #(.width(3)) comparator_14 (.a(FUNCT_3), .b(3'b000), .eq(comparator_14_eq));  // open: gt, lt
  Comparator #(.width(7)) comparator_15 (.a(undriven_3), .b({7{1'b0}}), .eq(comparator_15_eq));  // open: gt, lt
  Comparator #(.width(7)) comparator_16 (.a(undriven_4), .b(7'b0110011), .eq(comparator_16_eq));  // open: gt, lt
  Comparator #(.width(3)) comparator_17 (.a(FUNCT_3), .b(3'b000), .eq(comparator_17_eq));  // open: gt, lt
  Comparator #(.width(7)) comparator_18 (.a(undriven_3), .b(7'b0100000), .eq(comparator_18_eq));  // open: gt, lt
  Comparator #(.width(7)) comparator_19 (.a(undriven_4), .b(7'b0110011), .eq(comparator_19_eq));  // open: gt, lt
  Comparator #(.width(3)) comparator_20 (.a(FUNCT_3), .b(3'b111), .eq(comparator_20_eq));  // open: gt, lt
  Comparator #(.width(7)) comparator_21 (.a(undriven_4), .b(7'b0110011), .eq(comparator_21_eq));  // open: gt, lt
  Comparator #(.width(3)) comparator_22 (.a(FUNCT_3), .b(3'b110), .eq(comparator_22_eq));  // open: gt, lt
  Comparator #(.width(7)) comparator_23 (.a(undriven_4), .b(7'b0110011), .eq(comparator_23_eq));  // open: gt, lt
  Comparator #(.width(3)) comparator_24 (.a(FUNCT_3), .b(3'b010), .eq(comparator_24_eq));  // open: gt, lt
  Comparator #(.width(7)) comparator_25 (.a(undriven_4), .b(7'b0110011), .eq(comparator_25_eq));  // open: gt, lt
  Comparator #(.width(3)) comparator_26 (.a(FUNCT_3), .b(3'b100), .eq(comparator_26_eq));  // open: gt, lt
  Comparator #(.width(7)) comparator_27 (.a(undriven_4), .b(7'b1100011), .eq(comparator_27_eq));  // open: gt, lt
  Comparator #(.width(3)) comparator_28 (.a(FUNCT_3), .b(3'b000), .eq(comparator_28_eq));  // open: gt, lt
  // Text text_21: pin names not known
  Comparator #(.width(7)) comparator_29 (.a(undriven_4), .b(7'b0000011), .eq(comparator_29_eq));  // open: gt, lt
  Comparator #(.width(7)) comparator_30 (.a(undriven_4), .b(7'b0100011), .eq(comparator_30_eq));  // open: gt, lt
  or or_3 (or_3_out, comparator_12_eq, comparator_13_eq);
  and add (add_out, or_3_out, comparator_14_eq, comparator_15_eq);
  and sub (sub_out, comparator_16_eq, comparator_17_eq, comparator_18_eq);
  and AND_3 (AND_3_out, comparator_19_eq, comparator_20_eq);
  and OR_4 (OR_4_out, comparator_21_eq, comparator_22_eq);
  and SLT (SLT_out, comparator_23_eq, comparator_24_eq);
  and XOR (XOR_out, comparator_25_eq, comparator_26_eq);
  and BEQ (BEQ_out, comparator_27_eq, comparator_28_eq);
  and LW_SW (LW_SW_out, comparator_29_eq, comparator_30_eq);
  assign bit_extender_2_out = {{3{1'b0}}, add_out};  // Bit_Extender bit_extender_2
  assign bit_extender_3_out = {{3{1'b0}}, sub_out};  // Bit_Extender bit_extender_3
  assign bit_extender_4_out = {{3{1'b0}}, AND_3_out};  // Bit_Extender bit_extender_4
  assign bit_extender_5_out = {{3{1'b0}}, OR_4_out};  // Bit_Extender bit_extender_5
  assign bit_extender_6_out = {{3{1'b0}}, SLT_out};  // Bit_Extender bit_extender_6
  assign bit_extender_7_out = {{3{1'b0}}, XOR_out};  // Bit_Extender bit_extender_7
  assign bit_extender_8_out = {{3{1'b0}}, BEQ_out};  // Bit_Extender bit_extender_8
  assign bit_extender_9_out = {{3{1'b0}}, LW_SW_out};  // Bit_Extender bit_extender_9
  Multiplexer #(.select(4), .width(4), .enable("false")) multiplexer_6 (
    .in1(bit_extender_2_out), .in2(bit_extender_3_out), .in3(bit_extender_4_out), .in4(bit_extender_5_out),
    .in5(bit_extender_6_out), .in6(bit_extender_7_out), .in7(bit_extender_8_out), .in8(bit_extender_9_out),
    .out(multiplexer_6_out), .sel(in_6));  // open: in0, in9, in10, in11, in12, in13, in14, in15
  // Pins of 1 and 3 bits meet at control_decode_out_8
endmodule

module immediate_gen_2 (
  input  [31:0] Instruction,
  input  [31:0] in_2,
  input  [2:0] Instruction_Type,
  input  [31:0] in_4,
  input  [2:0] FUNCT_3,
  input  [2:0] in_6,
  input  [6:0] OP_CODE,
  input  [31:0] in_8,
  output [31:0] Immediate_Value,
  output [31:0] out_10,
  output [31:0] out_11,
  output [3:0] OUTPUT,
  output R_TYPE,
  output I_TYPE,
  output S_TYPE,
  output B_TYPE,
  output aui_pc,
  output J_TYPE,
  output lui,
  output [31:0] out_20
);

  wire add_out, AND_out, BEQ_out, comparator_1_eq, comparator_2_eq, comparator_3_eq, comparator_4_eq,
       comparator_5_eq, comparator_6_eq, comparator_14_eq, comparator_15_eq, comparator_16_eq,
       comparator_17_eq, comparator_18_eq, comparator_19_eq, comparator_20_eq, comparator_21_eq,
       comparator_22_eq, comparator_23_eq, comparator_24_eq, comparator_25_eq, comparator_26_eq,
       comparator_27_eq, comparator_28_eq, comparator_29_eq, comparator_30_eq, comparator_31_eq,
       comparator_32_eq, comparator_33_eq, comparator_34_eq, comparator_35_eq, comparator_36_eq,
       comparator_37_eq, LW_SW_out, or_1_out, or_2_out, OR_3_out, SLT_out, sub_out, undriven, XOR_out;
  wire [6:0] undriven_2, undriven_3;
  wire [31:0] bit_extender_6_out, bit_extender_7_out, bit_extender_8_out, bit_extender_9_out,
       bit_extender_10_out, bit_extender_11_out, bit_extender_12_out, bit_extender_13_out,
       bit_extender_14_out, bit_extender_15_out, bit_extender_16_out, bit_extender_17_out,
       bit_extender_18_out, bit_extender_19_out, bit_extender_20_out, multiplexer_1_out, multiplexer_2_out,
       multiplexer_3_out, multiplexer_4_out, multiplexer_5_out, multiplexer_6_out, multiplexer_7_out,
       multiplexer_8_out, multiplexer_9_out, multiplexer_10_out, multiplexer_11_out, multiplexer_12_out;

  Bit_Extender #(.in_width(12), .out_width(32), .\type ("one")) bit_extender_1 (.in(Instruction[31:20]));  // open: out
  Bit_Extender #(.in_width(12), .out_width(32), .\type ("one")) bit_extender_2 (.in({Instruction[31:25], Instruction[11:7]}));  // open: out
  Bit_Extender #(.in_width(12), .out_width(32), .\type ("one")) bit_extender_3 (.in({Instruction[31:25], Instruction[11:7]}));  // open: out
  Bit_Extender #(.in_width(20), .out_width(32), .\type ("one")) bit_extender_4 (.in(Instruction[31:12]));  // open: out
  Bit_Extender #(.in_width(12), .out_width(32), .\type ("one")) bit_extender_5 (.in(Instruction[30:19]));  // open: out
  assign bit_extender_6_out = {{20{1'b1}}, in_2[31:20]};  // Bit_Extender bit_extender_6
  assign bit_extender_7_out = {{20{1'b1}}, {in_2[31:25], in_2[11:7]}};  // Bit_Extender bit_extender_7
  assign bit_extender_8_out = {{20{1'b1}}, {in_2[31:25], in_2[11:7]}};  // Bit_Extender bit_extender_8
  assign bit_extender_9_out = {{12{1'b1}}, in_2[31:12]};  // Bit_Extender bit_extender_9
  assign bit_extender_10_out = {{20{1'b1}}, in_2[30:19]};  // Bit_Extender bit_extender_10
  assign bit_extender_11_out = {{20{1'b1}}, in_4[31:20]};  // Bit_Extender bit_extender_11
  assign bit_extender_12_out = {{20{1'b1}}, {in_4[31:25], in_4[11:7]}};  // Bit_Extender bit_extender_12
  assign bit_extender_13_out = {{20{1'b1}}, {in_4[31:25], in_4[11:7]}};  // Bit_Extender bit_extender_13
  assign bit_extender_14_out = {{12{1'b1}}, in_4[31:12]};  // Bit_Extender bit_extender_14
  assign bit_extender_15_out = {{20{1'b1}}, in_4[30:19]};  // Bit_Extender bit_extender_15
  assign bit_extender_16_out = {{20{1'b1}}, in_8[31:20]};  // Bit_Extender bit_extender_16
  assign bit_extender_17_out = {{20{1'b1}}, {in_8[31:25], in_8[11:7]}};  // Bit_Extender bit_extender_17
  assign bit_extender_18_out = {{20{1'b1}}, {in_8[31:25], in_8[11:7]}};  // Bit_Extender bit_extender_18
  assign bit_extender_19_out = {{12{1'b1}}, in_8[31:12]};  // Bit_Extender bit_extender_19
  assign bit_extender_20_out = {{20{1'b1}}, in_8[30:19]};  // Bit_Extender bit_extender_20
  Multiplexer #(.select(2), .width(32), .enable("false")) multiplexer_1 (
    .in1(bit_extender_6_out), .in3(bit_extender_7_out), .out(multiplexer_1_out), .sel(Instruction_Type[1:0]));  // open: in0, in2
  Multiplexer #(.width(32), .enable("false")) multiplexer_2 (
    .in0(bit_extender_11_out), .in1(bit_extender_12_out), .out(multiplexer_2_out), .sel(comparator_1_eq));
  Comparator #(.width(7)) comparator_1 (.a(in_4[6:0]), .b(7'b0010011), .eq(comparator_1_eq));  // open: gt, lt
  Comparator #(.width(7)) comparator_2 (.a(in_4[6:0]), .b(7'b0100011), .eq(comparator_2_eq));  // open: gt, lt
  Comparator #(.width(7)) comparator_3 (.a(in_4[6:0]), .b(7'b1100011), .eq(comparator_3_eq));  // open: gt, lt
  Comparator #(.width(7)) comparator_4 (.a(in_4[6:0]), .b(7'b0110111), .eq(comparator_4_eq));  // open: gt, lt
  Comparator #(.width(7)) comparator_5 (.a(in_4[6:0]), .b(7'b1101111), .eq(comparator_5_eq));  // open: gt, lt
  Comparator #(.width(7)) comparator_6 (.a(in_4[6:0]), .b(7'b0010111), .eq(comparator_6_eq));  // open: gt, lt
  Comparator #(.width(7)) comparator_7 (.a(OP_CODE), .b(7'b0110011), .eq(R_TYPE));  // open: gt, lt
  Comparator #(.width(7)) comparator_8 (.a(OP_CODE), .b(7'b0010011), .eq(I_TYPE));  // open: gt, lt
  Comparator #(.width(7)) comparator_9 (.a(OP_CODE), .b(7'b0100011), .eq(S_TYPE));  // open: gt, lt
  Comparator #(.width(7)) comparator_10 (.a(OP_CODE), .b(7'b1100011), .eq(B_TYPE), .lt(B_TYPE));  // open: gt
  Comparator #(.width(7)) comparator_11 (.a(OP_CODE), .b(7'b0110111), .eq(aui_pc));  // open: gt, lt
  Comparator #(.width(7)) comparator_12 (.a(OP_CODE), .b(7'b1101111), .eq(J_TYPE));  // open: gt, lt
  Comparator #(.width(7)) comparator_13 (.a(OP_CODE), .b(7'b0010001), .eq(lui));  // open: gt, lt
  Multiplexer #(.width(32), .enable("false")) multiplexer_3 (
    .in0(bit_extender_16_out), .in1(bit_extender_17_out), .out(multiplexer_3_out), .sel(comparator_14_eq));
  Comparator #(.width(7)) comparator_14 (.a(in_8[6:0]), .b(7'b0010011), .eq(comparator_14_eq));  // open: gt, lt
  Comparator #(.width(7)) comparator_15 (.a(in_8[6:0]), .b(7'b0100011), .eq(comparator_15_eq));  // open: gt, lt
  Comparator #(.width(7)) comparator_16 (.a(in_8[6:0]), .b(7'b1100011), .eq(comparator_16_eq));  // open: gt, lt
  Comparator #(.width(7)) comparator_17 (.a(in_8[6:0]), .b(7'b0110111), .eq(comparator_17_eq));  // open: gt, lt
  Comparator #(.width(7)) comparator_18 (.a(in_8[6:0]), .b(7'b1101111), .eq(comparator_18_eq));  // open: gt, lt
  Comparator #(.width(7)) comparator_19 (.a(in_8[6:0]), .b(7'b0010111), .eq(comparator_19_eq));  // open: gt, lt
  Multiplexer #(.width(32), .enable("false")) multiplexer_4 (
    .in0(bit_extender_8_out), .in1(bit_extender_9_out), .out(multiplexer_4_out));  // open: sel
  Multiplexer #(.width(32), .enable("false")) multiplexer_5 (
    .in0(bit_extender_13_out), .in1(bit_extender_14_out), .out(multiplexer_5_out), .sel(comparator_3_eq));
  Multiplexer #(.width(32), .enable("false")) multiplexer_6 (
    .in0(bit_extender_18_out), .in1(bit_extender_19_out), .out(multiplexer_6_out), .sel(comparator_16_eq));
  Multiplexer #(.width(32), .enable("false")) multiplexer_7 (
    .in0(multiplexer_1_out), .in1(multiplexer_4_out), .out(multiplexer_7_out), .sel(undriven));
  Multiplexer #(.width(32), .enable("false")) multiplexer_8 (
    .in0(multiplexer_4_out), .in1(bit_extender_10_out), .out(multiplexer_8_out));  // open: sel
  Multiplexer #(.width(32), .enable("false")) multiplexer_9 (
    .in0(multiplexer_2_out), .in1(multiplexer_5_out), .out(multiplexer_9_out), .sel(comparator_2_eq));
  Multiplexer #(.width(32), .enable("false")) multiplexer_10 (
    .in0(multiplexer_5_out), .in1(bit_extender_15_out), .out(multiplexer_10_out), .sel(or_1_out));
  or or_1 (or_1_out, comparator_4_eq, comparator_5_eq);
  Multiplexer #(.width(32), .enable("false")) multiplexer_11 (
    .in0(multiplexer_3_out), .in1(multiplexer_6_out), .out(multiplexer_11_out), .sel(comparator_15_eq));
  Multiplexer #(.width(32), .enable("false")) multiplexer_12 (
    .in0(multiplexer_6_out), .in1(bit_extender_20_out), .out(multiplexer_12_out), .sel(or_2_out));
  or or_2 (or_2_out, comparator_17_eq, comparator_18_eq);
  Multiplexer #(.width(32), .enable("false")) multiplexer_13 (
    .in0(multiplexer_7_out), .in1(multiplexer_8_out), .out(out_10));  // open: sel
  Multiplexer #(.width(32), .enable("false")) multiplexer_14 (
    .in0(multiplexer_9_out), .in1(multiplexer_10_out), .out(out_11), .sel(comparator_6_eq));
  Multiplexer #(.width(32), .enable("false")) multiplexer_15 (
    .in0(multiplexer_11_out), .in1(multiplexer_12_out), .out(out_20), .sel(comparator_19_eq));
  Comparator #(.width(7)) comparator_20 (.a(undriven_3), .b(7'b0110011), .eq(comparator_20_eq));  // open: gt, lt
  Comparator #(.width(3)) comparator_21 (.a(FUNCT_3), .b(3'b000), .eq(comparator_21_eq));  // open: gt, lt
  Comparator #(.width(7)) comparator_22 (.a(undriven_2), .b({7{1'b0}}), .eq(comparator_22_eq));  // open: gt, lt
  Comparator #(.width(7)) comparator_23 (.a(undriven_3), .b(7'b0110011), .eq(comparator_23_eq));  // open: gt, lt
  Comparator #(.width(3)) comparator_24 (.a(FUNCT_3), .b(3'b000), .eq(comparator_24_eq));  // open: gt, lt
  Comparator #(.width(7)) comparator_25 (.a(undriven_2), .b(7'b0100000), .eq(comparator_25_eq));  // open: gt, lt
  Comparator #(.width(7)) comparator_26 (.a(undriven_3), .b(7'b0110011), .eq(comparator_26_eq));  // open: gt, lt
  Comparator #(.width(3)) comparator_27 (.a(FUNCT_3), .b(3'b111), .eq(comparator_27_eq));  // open: gt, lt
  Comparator #(.width(7)) comparator_28 (.a(undriven_3), .b(7'b0110011), .eq(comparator_28_eq));  // open: gt, lt
  Comparator #(.width(3)) comparator_29 (.a(FUNCT_3), .b(3'b110), .eq(comparator_29_eq));  // open: gt, lt
  Comparator #(.width(7)) comparator_30 (.a(undriven_3), .b(7'b0110011), .eq(comparator_30_eq));  // open: gt, lt
  Comparator #(.width(3)) comparator_31 (.a(FUNCT_3), .b(3'b010), .eq(comparator_31_eq));  // open: gt, lt
  Comparator #(.width(7)) comparator_32 (.a(undriven_3), .b(7'b0110011), .eq(comparator_32_eq));  // open: gt, lt
  Comparator #(.width(3)) comparator_33 (.a(FUNCT_3), .b(3'b100), .eq(comparator_33_eq));  // open: gt, lt
  Comparator #(.width(7)) comparator_34 (.a(undriven_3), .b(7'b1100011), .eq(comparator_34_eq));  // open: gt, lt
  Comparator #(.width(3)) comparator_35 (.a(FUNCT_3), .b(3'b000), .eq(comparator_35_eq));  // open: gt, lt
  Comparator #(.width(7)) comparator_36 (.a(undriven_3), .b(7'b0000011), .eq(comparator_36_eq));  // open: gt, lt
  Comparator #(.width(7)) comparator_37 (.a(undriven_3), .b(7'b0100011), .eq(comparator_37_eq));  // open: gt, lt
  // Text text_1: pin names not known
  and add (add_out, comparator_20_eq, comparator_21_eq, comparator_22_eq);
  and sub (sub_out, comparator_23_eq, comparator_24_eq, comparator_25_eq);
  and AND (AND_out, comparator_26_eq, comparator_27_eq);
  and OR_3 (OR_3_out, comparator_28_eq, comparator_29_eq);
  and SLT (SLT_out, comparator_30_eq, comparator_31_eq);
  and XOR (XOR_out, comparator_32_eq, comparator_33_eq);
  and BEQ (BEQ_out, comparator_34_eq, comparator_35_eq);
  and LW_SW (LW_SW_out, comparator_36_eq, comparator_37_eq);
  Decoder #(.select(3), .enable("false")) decoder_1 (
    .out0(add_out), .out1(sub_out), .out2(AND_out), .out3(OR_3_out), .out4(SLT_out), .out5(XOR_out),
    .out6(BEQ_out), .out7(LW_SW_out), .sel(in_6));
  Multiplexer #(.select(3), .width(4), .enable("false")) multiplexer_16 (
    .in0(4'b0010), .in1(4'b0110), .in2(4'b0000), .in3(4'b0001), .in4(4'b0111), .in5(4'b0011), .in6(4'b0110),
    .in7(4'b0010), .out(OUTPUT), .sel(in_6));
  // Pins of 2 and 3 bits meet at Instruction_Type
endmodule

module immediate_gen_3 (
  input  [31:0] ins,
  output [31:0] IMM
);

  wire comparator_1_eq, comparator_2_eq, comparator_3_eq, comparator_4_eq, comparator_5_eq, comparator_6_eq,
       comparator_7_eq, comparator_8_eq, comparator_9_eq, comparator_10_eq, comparator_11_eq, or_1_out,
       or_2_out;
  wire [11:0] multiplexer_1_out, multiplexer_2_out, multiplexer_3_out;
  wire [19:0] multiplexer_4_out;
  wire [31:0] bit_extender_1_out, bit_extender_2_out, bit_extender_3_out, bit_extender_4_out,
       bit_extender_5_out, multiplexer_5_out, multiplexer_6_out, multiplexer_7_out, multiplexer_8_out;

  Comparator #(.width(7)) comparator_1 (.a(7'b0000011), .b(ins[6:0]), .eq(comparator_1_eq));  // open: gt, lt
  Comparator #(.width(7)) comparator_2 (.a(7'b0001111), .b(ins[6:0]), .eq(comparator_2_eq));  // open: gt, lt
  Comparator #(.width(7)) comparator_3 (.a(7'b0010011), .b(ins[6:0]), .eq(comparator_3_eq));  // open: gt, lt
  Comparator #(.width(7)) comparator_4 (.a(7'b0011011), .b(ins[6:0]), .eq(comparator_4_eq));  // open: gt, lt
  Comparator #(.width(7)) comparator_5 (.a(7'b1100111), .b(ins[6:0]), .eq(comparator_5_eq));  // open: gt, lt
  Comparator #(.width(7)) comparator_6 (.a(7'b1110011), .b(ins[6:0]), .eq(comparator_6_eq));  // open: gt, lt
  Comparator #(.width(7)) comparator_7 (.a(7'b0100011), .b(ins[6:0]), .eq(comparator_7_eq));  // open: gt, lt
  Comparator #(.width(7)) comparator_8 (.a(7'b1100011), .b(ins[6:0]), .eq(comparator_8_eq));  // open: gt, lt
  Comparator #(.width(7)) comparator_9 (.a(7'b0010111), .b(ins[6:0]), .eq(comparator_9_eq));  // open: gt, lt
  Comparator #(.width(7)) comparator_10 (.a(7'b0110111), .b(ins[6:0]), .eq(comparator_10_eq));  // open: gt, lt
  Comparator #(.width(7)) comparator_11 (.a(7'b1101111), .b(ins[6:0]), .eq(comparator_11_eq));  // open: gt, lt
  or or_1 (or_1_out, comparator_1_eq, comparator_2_eq, comparator_3_eq, comparator_4_eq, comparator_5_eq, comparator_6_eq);
  or or_2 (or_2_out, comparator_9_eq, comparator_10_eq);
  Multiplexer #(.width(12), .enable("false")) multiplexer_1 (
    .in1(ins[31:20]), .out(multiplexer_1_out), .sel(or_1_out));  // open: in0
  Multiplexer #(.width(12), .enable("false")) multiplexer_2 (
    .in1({ins[31:25], ins[11:7]}), .out(multiplexer_2_out), .sel(comparator_7_eq));  // open: in0
  Multiplexer #(.width(12), .enable("false")) multiplexer_3 (
    .in1({ins[31:25], ins[11:7]}), .out(multiplexer_3_out), .sel(comparator_8_eq));  // open: in0
  Multiplexer #(.width(20), .enable("false")) multiplexer_4 (
    .in1(ins[31:12]), .out(multiplexer_4_out), .sel(or_2_out));  // open: in0
  assign bit_extender_1_out = {{20{multiplexer_1_out[11]}}, multiplexer_1_out};  // Bit_Extender bit_extender_1
  assign bit_extender_2_out = {{20{multiplexer_2_out[11]}}, multiplexer_2_out};  // Bit_Extender bit_extender_2
  assign bit_extender_3_out = {{20{multiplexer_3_out[11]}}, multiplexer_3_out};  // Bit_Extender bit_extender_3
  assign bit_extender_4_out = {{12{multiplexer_4_out[19]}}, multiplexer_4_out};  // Bit_Extender bit_extender_4
  Multiplexer #(.width(32), .enable("false")) multiplexer_5 (
    .in0(bit_extender_1_out), .in1(bit_extender_2_out), .out(multiplexer_5_out), .sel(comparator_7_eq));
  assign bit_extender_5_out = {{11{ins[31]}}, {ins[31], ins[19:12], ins[20], ins[30:21], 1'b0}};  // Bit_Extender bit_extender_5
  Multiplexer #(.width(32), .enable("false")) multiplexer_6 (
    .in0(multiplexer_5_out), .in1(bit_extender_3_out), .out(multiplexer_6_out), .sel(comparator_8_eq));
  Multiplexer #(.width(32), .enable("false")) multiplexer_7 (
    .in1(bit_extender_5_out), .out(multiplexer_7_out), .sel(comparator_11_eq));  // open: in0
  Multiplexer #(.width(32), .enable("false")) multiplexer_8 (
    .in0(multiplexer_6_out), .in1(bit_extender_4_out), .out(multiplexer_8_out), .sel(or_2_out));
  Multiplexer #(.width(32), .enable("false")) multiplexer_9 (
    .in0(multiplexer_8_out), .in1(multiplexer_7_out), .out(IMM), .sel(comparator_11_eq));
endmodule

module Data_Memory (
  input  [31:0] ADDRESS,
  input  [31:0] WRITE_DATA,
  input  SEL,
  input  MEM_WRITE_SEL,
  input  CLOCK,
  input  CLEAR,
  input  MEM_READ_SEL,
  output [31:0] READDATA
);

  RAM #(.dataWidth(32), .bus("separate")) ram_1 (
    .addr(ADDRESS[7:0]), .din(WRITE_DATA), .data(READDATA), .str(MEM_WRITE_SEL), .sel(SEL), .clk(CLOCK),
    .ld(MEM_READ_SEL), .clr(CLEAR));
endmodule

module main_2 (
  input  in_1,
  input  in_2
);

  wire ALU_With_Branch_out_5, and_1_out, clock_1_out, control_decode_out_2, control_decode_out_3,
       control_decode_out_5, control_decode_out_6, control_decode_out_7, control_decode_out_9, or_1_out,
       or_2_out;
  wire [2:0] control_decode_out_8;
  wire [3:0] ALUControl_output, TYPE_DECODER_out_2;
  wire [6:0] ram_1_data;
  wire [31:0] adder_1_out, adder_2_out, ALU_With_Branch_out_6, immediate_gen_3_1_imm, multiplexer_1_out,
       multiplexer_3_out, register_1_q, Register_file_p1, Register_file_p7, Register_file_p8, text_2_p8;
  wire [31:7] ram_1_data_2;

  Register #(.width(32)) register_1 (.D(multiplexer_3_out), .en(in_1), .Q(register_1_q), .clk(clock_1_out), .clr(in_2));
  Clock clock_1 (.out(clock_1_out));
  control_decode control_decode (
    .in_1(ram_1_data), .out_2(control_decode_out_2), .out_3(control_decode_out_3),
    .out_5(control_decode_out_5), .out_6(control_decode_out_6), .out_7(control_decode_out_7),
    .out_8(control_decode_out_8[0]), .out_9(control_decode_out_9));  // open: out_4
  RAM #(.addrWidth(24), .dataWidth(32)) ram_1 (
    .addr(register_1_q[25:2]), .data({ram_1_data_2, ram_1_data}), .sel(in_1), .clk(clock_1_out), .clr(in_2));  // open: ld
  immediate_gen_3 immediate_gen_3_1 (.ins({ram_1_data_2, ram_1_data}), .IMM(immediate_gen_3_1_imm));
  Type_decoder TYPE_DECODER (.OP_CODE(ram_1_data), .out_2(TYPE_DECODER_out_2));  // open: out_3
  // Register_File Register_file: pin names not known; wires that end beside it: Register_file_p1, clock_1_out, control_decode_out_2, ram_1_data_2[11:7], ram_1_data_2[19:15], ram_1_data_2[24:20], Register_file_p7, Register_file_p8
  ALU_CONTROL ALUControl (
    .OPCODE(ram_1_data), .FUNCT_3(ram_1_data_2[14:12]), .FUNCT_7(ram_1_data_2[31:25]),
    .in_4(TYPE_DECODER_out_2), .OUTPUT(ALUControl_output));
  // Text text_1: pin names not known
  Multiplexer #(.width(32), .enable("false")) multiplexer_1 (
    .in0(Register_file_p8), .in1(immediate_gen_3_1_imm), .out(multiplexer_1_out), .sel(control_decode_out_3));
  ALU_With_branch ALU_With_Branch (
    .A(Register_file_p7), .B(multiplexer_1_out), .ALUOp(ALUControl_output),
    .BranchType(control_decode_out_8), .out_5(ALU_With_Branch_out_5), .out_6(ALU_With_Branch_out_6));
  and and_1 (and_1_out, control_decode_out_8[2], ALU_With_Branch_out_5);
  or or_1 (or_1_out, control_decode_out_7, and_1_out);
  // Text text_2: pin names not known; wires that end beside it: ALU_With_Branch_out_6, Register_file_p8, in_1, in_2, clock_1_out, control_decode_out_6, control_decode_out_5, text_2_p8
  Multiplexer #(.width(32), .enable("false")) multiplexer_2 (
    .in0(ALU_With_Branch_out_6), .in1(text_2_p8), .out(Register_file_p1), .sel(control_decode_out_7));
  Adder #(.width(32)) adder_1 (.a(32'h4), .b(register_1_q), .out(adder_1_out));  // open: cin, cout
  Adder #(.width(32)) adder_2 (.a(register_1_q), .b(immediate_gen_3_1_imm), .out(adder_2_out));  // open: cin, cout
  // Text text_3: pin names not known
  Multiplexer #(.width(32), .enable("false")) multiplexer_3 (
    .in0(adder_1_out), .in1(adder_2_out), .out(multiplexer_3_out), .sel(or_2_out));
  or or_2 (or_2_out, or_1_out, control_decode_out_9);
  // Pins of 1 and 3 bits meet at control_decode_out_8
endmodule

module alu (
  input  [6:0] OPCODE,
  input  [2:0] FUNCT_3,
  input  [6:0] FUNCT_7,
  input  [31:0] A,
  input  [2:0] BranchType,
  input  [31:0] B,
  input  [3:0] ALUOp,
  input  [2:0] in_8,
  output out_9,
  output [31:0] out_10,
  output [3:0] OUTPUT
);

  wire BRANCH_out, comparator_1_eq, comparator_2_eq, comparator_3_eq, comparator_4_eq, comparator_5_eq,
       comparator_6_eq, comparator_7_eq, comparator_8_eq, comparator_9_eq, comparator_10_eq,
       comparator_11_eq, comparator_12_eq, comparator_13_eq, comparator_14_eq, comparator_15_eq,
       comparator_16_eq, comparator_17_eq, comparator_18_eq, comparator_19_eq, comparator_20_eq,
       comparator_21_eq, comparator_22_eq, comparator_23_eq, comparator_24_eq, comparator_25_eq,
       comparator_26_eq, comparator_27_eq, comparator_28_eq, comparator_29_eq, comparator_30_eq,
       comparator_31_eq, comparator_32_eq, comparator_33_eq, comparator_34_eq, comparator_35_eq,
       comparator_36_eq, comparator_37_eq, comparator_38_eq, comparator_39_eq, comparator_40_eq,
       comparator_41_eq, comparator_42_eq, comparator_43_eq, comparator_44_eq, comparator_45_eq,
       comparator_46_eq, comparator_47_eq, I_Type_ALU_out, JUMP_out, LOAD_out, multiplexer_2_out, not_1_out,
       not_2_out, not_3_out, or_1_out, or_2_out, or_3_out, or_4_out, or_5_out, or_6_out, or_7_out, or_8_out,
       R_Type_ALU_out, STORE_out, upper_imm_out;
  wire [3:0] bit_extender_1_out, bit_extender_2_out, bit_extender_3_out, bit_extender_4_out,
       bit_extender_5_out, bit_extender_6_out, bit_extender_7_out;
  wire [31:0] adder_1_out, and_1_out, bit_extender_8_out, bit_extender_9_out, or_9_out, shifter_1_out,
       shifter_2_out, shifter_3_out, subtractor_1_out, subtractor_2_out, xor_1_out;

  Comparator #(.width(7)) comparator_1 (.a(OPCODE), .b(7'b0000011), .eq(comparator_1_eq));  // open: gt, lt
  // Text text_1: pin names not known
  Comparator #(.width(3)) comparator_2 (.a(FUNCT_3), .b(3'b000), .eq(comparator_2_eq));  // open: gt, lt
  // Text text_2: pin names not known
  Comparator #(.width(3)) comparator_3 (.a(FUNCT_3), .b(3'b001), .eq(comparator_3_eq));  // open: gt, lt
  // Text text_3: pin names not known
  Comparator #(.width(3)) comparator_4 (.a(FUNCT_3), .b(3'b010), .eq(comparator_4_eq));  // open: gt, lt
  // Text text_4: pin names not known
  Comparator #(.width(3)) comparator_5 (.a(FUNCT_3), .b(3'b100), .eq(comparator_5_eq));  // open: gt, lt
  // Text text_5: pin names not known
  Comparator #(.width(3)) comparator_6 (.a(FUNCT_3), .b(3'b101), .eq(comparator_6_eq));  // open: gt, lt
  Comparator #(.width(7)) comparator_7 (.a(OPCODE), .b(7'b0100011), .eq(comparator_7_eq));  // open: gt, lt
  // Text text_6: pin names not known
  Comparator #(.width(3)) comparator_8 (.a(FUNCT_3), .b(3'b000), .eq(comparator_8_eq));  // open: gt, lt
  // Text text_7: pin names not known
  Comparator #(.width(3)) comparator_9 (.a(FUNCT_3), .b(3'b001), .eq(comparator_9_eq));  // open: gt, lt
  Comparator #(.width(3)) comparator_10 (.a(FUNCT_3), .b(3'b010), .eq(comparator_10_eq));  // open: gt, lt
  Comparator #(.width(7)) comparator_11 (.a(OPCODE), .b(7'b1100011), .eq(comparator_11_eq));  // open: gt, lt
  // Text text_8: pin names not known
  Comparator #(.width(3)) comparator_12 (.a(FUNCT_3), .b(3'b000), .eq(comparator_12_eq));  // open: gt, lt
  // Text text_9: pin names not known
  Comparator #(.width(3)) comparator_13 (.a(FUNCT_3), .b(3'b001), .eq(comparator_13_eq));  // open: gt, lt
  // Text text_10: pin names not known
  Comparator #(.width(3)) comparator_14 (.a(FUNCT_3), .b(3'b100), .eq(comparator_14_eq));  // open: gt, lt
  // Text text_11: pin names not known
  Comparator #(.width(3)) comparator_15 (.a(FUNCT_3), .b(3'b101), .eq(comparator_15_eq));  // open: gt, lt
  // Text text_12: pin names not known
  Comparator #(.width(3)) comparator_16 (.a(FUNCT_3), .b(3'b110), .eq(comparator_16_eq));  // open: gt, lt
  // Text text_13: pin names not known
  Comparator #(.width(3)) comparator_17 (.a(FUNCT_3), .b(3'b111), .eq(comparator_17_eq));  // open: gt, lt
  // Text text_14: pin names not known
  Comparator #(.width(7)) comparator_18 (.a(OPCODE), .b(7'b1101111), .eq(comparator_18_eq));  // open: gt, lt
  // Text text_15: pin names not known
  Comparator #(.width(7)) comparator_19 (.a(OPCODE), .b(7'b1100111), .eq(comparator_19_eq));  // open: gt, lt
  Comparator #(.width(3)) comparator_20 (.a(FUNCT_3), .b(3'b000), .eq(comparator_20_eq));  // open: gt, lt
  // Text text_16: pin names not known
  Comparator #(.width(7)) comparator_21 (.a(OPCODE), .b(7'b0110111), .eq(comparator_21_eq));  // open: gt, lt
  // Text text_17: pin names not known
  Comparator #(.width(7)) comparator_22 (.a(OPCODE), .b(7'b0010111), .eq(comparator_22_eq));  // open: gt, lt
  Comparator #(.width(7)) comparator_23 (.a(OPCODE), .b(7'b0110011), .eq(comparator_23_eq));  // open: gt, lt
  Comparator #(.width(3)) comparator_24 (.a(FUNCT_3), .b(3'b000), .eq(comparator_24_eq));  // open: gt, lt
  Comparator #(.width(3)) comparator_25 (.a(FUNCT_3), .b(3'b111), .eq(comparator_25_eq));  // open: gt, lt
  Comparator #(.width(3)) comparator_26 (.a(FUNCT_3), .b(3'b110), .eq(comparator_26_eq));  // open: gt, lt
  Comparator #(.width(3)) comparator_27 (.a(FUNCT_3), .b(3'b100), .eq(comparator_27_eq));  // open: gt, lt
  Comparator #(.width(3)) comparator_28 (.a(FUNCT_3), .b(3'b001), .eq(comparator_28_eq));  // open: gt, lt
  Comparator #(.width(3)) comparator_29 (.a(FUNCT_3), .b(3'b101), .eq(comparator_29_eq));  // open: gt, lt
  Comparator #(.width(3)) comparator_30 (.a(FUNCT_3), .b(3'b010), .eq(comparator_30_eq));  // open: gt, lt
  Comparator #(.width(3)) comparator_31 (.a(FUNCT_3), .b(3'b011), .eq(comparator_31_eq));  // open: gt, lt
  Comparator #(.width(7)) comparator_32 (.a(FUNCT_7), .b({7{1'b0}}), .eq(comparator_32_eq));  // open: gt, lt
  Comparator #(.width(7)) comparator_33 (.a(FUNCT_7), .b(7'b0100000), .eq(comparator_33_eq));  // open: gt, lt
  Comparator #(.width(7)) comparator_34 (.a(OPCODE), .b(7'b0010011), .eq(comparator_34_eq));  // open: gt, lt
  Comparator #(.width(3)) comparator_35 (.a(FUNCT_3), .b(3'b000), .eq(comparator_35_eq));  // open: gt, lt
  Comparator #(.width(3)) comparator_36 (.a(FUNCT_3), .b(3'b111), .eq(comparator_36_eq));  // open: gt, lt
  Comparator #(.width(3)) comparator_37 (.a(FUNCT_3), .b(3'b110), .eq(comparator_37_eq));  // open: gt, lt
  Comparator #(.width(3)) comparator_38 (.a(FUNCT_3), .b(3'b100), .eq(comparator_38_eq));  // open: gt, lt
  Comparator #(.width(3)) comparator_39 (.a(FUNCT_3), .b(3'b001), .eq(comparator_39_eq));  // open: gt, lt
  Comparator #(.width(3)) comparator_40 (.a(FUNCT_3), .b(3'b101), .eq(comparator_40_eq));  // open: gt, lt
  Comparator #(.width(3)) comparator_41 (.a(FUNCT_3), .b(3'b010), .eq(comparator_41_eq));  // open: gt, lt
  Comparator #(.width(3)) comparator_42 (.a(FUNCT_3), .b(3'b011), .eq(comparator_42_eq));  // open: gt, lt
  Comparator #(.width(7)) comparator_43 (.a(FUNCT_7), .b({7{1'b0}}), .eq(comparator_43_eq));  // open: gt, lt
  Comparator #(.width(7)) comparator_44 (.a(FUNCT_7), .b(7'b0100000), .eq(comparator_44_eq));  // open: gt, lt
  // Text text_18: pin names not known
  or or_1 (or_1_out, comparator_18_eq, comparator_19_eq);
  or upper_imm (upper_imm_out, comparator_21_eq, comparator_22_eq);
  // Text text_19: pin names not known
  // Text text_20: pin names not known
  // Text text_21: pin names not known
  // Text text_22: pin names not known
  // Text text_23: pin names not known
  // Text text_24: pin names not known
  // Text text_25: pin names not known
  // Text text_26: pin names not known
  // Text text_27: pin names not known
  // Text text_28: pin names not known
  or or_2 (or_2_out, comparator_32_eq, comparator_33_eq);
  // Text text_29: pin names not known
  // Text text_30: pin names not known
  // Text text_31: pin names not known
  // Text text_32: pin names not known
  // Text text_33: pin names not known
  // Text text_34: pin names not known
  // Text text_35: pin names not known
  // Text text_36: pin names not known
  // Text text_37: pin names not known
  or or_3 (or_3_out, comparator_2_eq, comparator_3_eq, comparator_4_eq, comparator_5_eq, comparator_6_eq);
  or or_4 (or_4_out, comparator_8_eq, comparator_9_eq, comparator_10_eq);
  or or_5 (or_5_out, comparator_12_eq, comparator_13_eq, comparator_14_eq, comparator_15_eq, comparator_16_eq, comparator_17_eq);
  or or_6 (or_6_out, comparator_24_eq, comparator_25_eq, comparator_26_eq, comparator_27_eq, comparator_28_eq, comparator_29_eq, comparator_30_eq, comparator_31_eq);
  or or_7 (or_7_out, comparator_35_eq, comparator_36_eq, comparator_37_eq, comparator_38_eq, comparator_39_eq, comparator_40_eq, comparator_41_eq, comparator_42_eq);
  or or_8 (or_8_out, comparator_43_eq, comparator_44_eq);
  and R_Type_ALU (R_Type_ALU_out, comparator_23_eq, or_6_out, or_2_out);
  and LOAD (LOAD_out, comparator_1_eq, or_3_out);
  and STORE (STORE_out, comparator_7_eq, or_4_out);
  and BRANCH (BRANCH_out, comparator_11_eq, or_5_out);
  and JUMP (JUMP_out, or_1_out, comparator_20_eq);
  assign bit_extender_1_out = {{3{1'b0}}, R_Type_ALU_out};  // Bit_Extender bit_extender_1
  and I_Type_ALU (I_Type_ALU_out, comparator_34_eq, or_7_out, or_8_out);
  assign bit_extender_2_out = {{3{1'b0}}, LOAD_out};  // Bit_Extender bit_extender_2
  assign bit_extender_3_out = {{3{1'b0}}, STORE_out};  // Bit_Extender bit_extender_3
  assign bit_extender_4_out = {{3{1'b0}}, BRANCH_out};  // Bit_Extender bit_extender_4
  assign bit_extender_5_out = {{3{1'b0}}, JUMP_out};  // Bit_Extender bit_extender_5
  assign bit_extender_6_out = {{3{1'b0}}, upper_imm_out};  // Bit_Extender bit_extender_6
  assign bit_extender_7_out = {{3{1'b0}}, I_Type_ALU_out};  // Bit_Extender bit_extender_7
  Multiplexer #(.select(3), .width(4), .enable("false")) multiplexer_1 (
    .in0(bit_extender_1_out), .in1(bit_extender_1_out), .in2(bit_extender_7_out), .in3(bit_extender_2_out),
    .in4(bit_extender_3_out), .in5(bit_extender_4_out), .in6(bit_extender_5_out), .in7(bit_extender_6_out),
    .out(OUTPUT), .sel(in_8));
  // Text text_38: pin names not known
  Adder #(.width(32)) adder_1 (.a(A), .b(B), .out(adder_1_out));  // open: cin, cout
  // Text text_39: pin names not known
  Subtractor #(.width(32)) subtractor_1 (.a(A), .b(B), .out(subtractor_1_out));  // open: bin, bout
  // Text text_40: pin names not known
  assign and_1_out = A & B;  // AND_Gate and_1, 32 bits wide
  // Text text_41: pin names not known
  assign or_9_out = A | B;  // OR_Gate or_9, 32 bits wide
  // Text text_42: pin names not known
  assign xor_1_out = A ^ B;  // XOR_Gate xor_1, 32 bits wide
  // Text text_43: pin names not known
  Shifter #(.width(32)) shifter_1 (.in(A), .\dist (B[4:0]), .out(shifter_1_out));
  // Text text_44: pin names not known
  Shifter #(.width(32), .shift("lr")) shifter_2 (.in(A), .\dist (B[4:0]), .out(shifter_2_out));
  // Text text_45: pin names not known
  Shifter #(.width(32), .shift("ar")) shifter_3 (.in(A), .\dist (B[4:0]), .out(shifter_3_out));
  // Text text_46: pin names not known
  Subtractor #(.width(32)) subtractor_2 (.a(A), .b(B), .out(subtractor_2_out));  // open: bin, bout
  // Text text_47: pin names not known; wires that end beside it: B
  Comparator #(.width(32)) comparator_45 (.a(A), .b(B), .eq(comparator_45_eq));  // open: gt, lt
  Multiplexer #(.enable("false")) multiplexer_2 (
    .in0(1'b1), .in1(1'b0), .out(multiplexer_2_out), .sel(comparator_45_eq));
  Comparator #(.width(32)) comparator_46 (.a(subtractor_1_out), .b({32{1'b0}}), .eq(comparator_46_eq));  // open: gt, lt
  assign bit_extender_8_out = {{31{1'b0}}, multiplexer_2_out};  // Bit_Extender bit_extender_8
  assign bit_extender_9_out = {{31{1'b0}}, comparator_46_eq};  // Bit_Extender bit_extender_9
  Multiplexer #(.select(4), .width(32), .enable("false")) multiplexer_3 (
    .in0(adder_1_out), .in1(adder_1_out), .in2(bit_extender_9_out), .in3(subtractor_1_out), .in4(and_1_out),
    .in5(or_9_out), .in6(xor_1_out), .in7(shifter_1_out), .in8(shifter_2_out), .in9(shifter_3_out),
    .in10(subtractor_2_out), .in11(bit_extender_8_out), .in12({32{1'b0}}), .in13({32{1'b0}}),
    .in14({32{1'b0}}), .in15({32{1'b0}}), .out(out_10), .sel(ALUOp));
  Comparator #(.width(32)) comparator_47 (.a(subtractor_1_out), .b({32{1'b0}}), .eq(comparator_47_eq));  // open: gt, lt
  not not_1 (not_1_out, comparator_47_eq);
  not not_2 (not_2_out, subtractor_2_out[1]);
  not not_3 (not_3_out, multiplexer_2_out);
  Multiplexer #(.select(3), .enable("false")) multiplexer_4 (
    .in0(comparator_47_eq), .in1(not_1_out), .in2(subtractor_2_out[1]), .in3(not_2_out),
    .in4(multiplexer_2_out), .in5(not_3_out), .in6(1'b0), .in7(1'b0), .out(out_9), .sel(BranchType));
endmodule
